// Digital circuit TESTES.dig as structural Verilog
module TESTES (
  input  clock
);

  wire and_1_out, and_2_out, and_3_out, and_4_out, not_1_out, not_2_out, not_3_out, or_1_out,
       ula_32bits_1_neg, ula_32bits_1_zero;
  wire [3:0] MI_d_2;
  wire [6:0] CONTROLE_d;
  wire [27:0] MI_d;
  wire [31:0] add_1_s, add_2_s, bitextender_1_out, DADOS_d, multiplexer_1_out, multiplexer_3_out, PC_q,
       regs_1_p4, regs_1_p7, regs_1_p8, ula_32bits_1_r;

  D_FF #(.Bits(32)) PC (.D(multiplexer_3_out), .C(clock), .Q(PC_q));  // open: nQ
  Add #(.Bits(32)) add_1 (.a(32'h1), .b(PC_q), .c_i(1'b0), .s(add_1_s));  // open: c_o
  ROM #(.AddrBits(24), .isProgramMemory("true"), .Bits(32)) MI (.A(PC_q[23:0]), .sel(1'b1), .D({MI_d_2, MI_d}));
  ROM #(.AddrBits(4), .Bits(7)) CONTROLE (.A(MI_d_2), .sel(1'b1), .D(CONTROLE_d));
  BitExtender #(.inputBits(16), .outputBits(32)) bitextender_1 (.in(MI_d[15:0]), .out(bitextender_1_out));
  // regs regs_1: pin names not known; wires that end beside it: MI_d[27:24], MI_d[23:20], MI_d[19:16], regs_1_p4, CONTROLE_d[1], clock, regs_1_p7, regs_1_p8
  Multiplexer #(.Bits(32)) multiplexer_1 (
    .sel(CONTROLE_d[3]), .in_0(regs_1_p8), .in_1(bitextender_1_out), .out(multiplexer_1_out));
  Multiplexer #(.Bits(32)) multiplexer_2 (.sel(CONTROLE_d[2]), .in_0(ula_32bits_1_r), .in_1(DADOS_d), .out(regs_1_p4));
  Add #(.Bits(32)) add_2 (.a(add_1_s), .b(bitextender_1_out), .c_i(1'b0), .s(add_2_s));  // open: c_o
  ula_32bits ula_32bits_1 (
    .R(ula_32bits_1_r), .zero(ula_32bits_1_zero), .neg(ula_32bits_1_neg), .F(CONTROLE_d[6:4]), .A(regs_1_p7),
    .B(multiplexer_1_out));  // open: overflow
  and and_1 (and_1_out, CONTROLE_d[4], ula_32bits_1_zero);
  Multiplexer #(.Bits(32)) multiplexer_3 (.sel(or_1_out), .in_0(add_1_s), .in_1(add_2_s), .out(multiplexer_3_out));
  or or_1 (or_1_out, and_1_out, and_2_out);
  and and_2 (and_2_out, CONTROLE_d[4], ula_32bits_1_neg);
  RAMDualPort #(.AddrBits(24), .Bits(32)) DADOS (
    .A(ula_32bits_1_r[23:0]), .Din(regs_1_p8), .str(and_3_out), .C(clock), .ld(not_3_out), .D(DADOS_d));
  and and_3 (and_3_out, not_3_out, CONTROLE_d[0]);
  not not_1 (not_1_out, MI_d_2[2]);
  not not_2 (not_2_out, MI_d_2[0]);
  not not_3 (not_3_out, and_4_out);
  and and_4 (and_4_out, ula_32bits_1_r[24], ula_32bits_1_r[25], ula_32bits_1_r[26], ula_32bits_1_r[27], ula_32bits_1_r[28], ula_32bits_1_r[29], ula_32bits_1_r[30], ula_32bits_1_r[31], not_2_out, MI_d_2[1], not_1_out, MI_d_2[3]);
  Terminal #(.termWidth(80), .termHeight(24)) TERMINAL (.D(regs_1_p8), .C(clock), .en(and_4_out));

  // Notes on the sheet:
  //   TEM ALGUNS ERROS AINDA
  //   MAS FUNCIONA! 
  //   ALTEREI A ROM E CONTROLE
  //   PC + 1
  //   contents of MI (hex, n*v repeats v):
  //   8001cafe,8002dead,1230000,8006000c,a6300000,a6200001,96070001
  //   ,800dff00,80070041,ad700000,8005ffff,8007ffff,a5700000,8009fafa
  //   ,8008fefe,c9800001
  //   CONTROLE
  //   contents of CONTROLE (hex, n*v repeats v):
  //   2,12,22,32,42,0,0,0,a,e,10,0,10
  //   BEQ & BLT
  //   wrReg
  //   selB
  //   PODE SER TROCADO POR UM MUX
  //   aluFunc
  //   selC
  //   ULA
  //   wrMem
  //   MD
  //   TERMINAL
endmodule
