// Digital circuit ula_backup.dig as structural Verilog
module ula_backup (
  input  [2:0] F,
  input  [31:0] A,
  input  [31:0] B,
  input  [2:0] F_2,
  input  [31:0] A_2,
  input  [31:0] B_2,
  output neg,
  output overflow,
  output zero,
  output [31:0] R,
  output neg_2,
  output overflow_2,
  output zero_2,
  output [31:0] R_2
);

  wire and_3_out, and_4_out, and_5_out, and_6_out, and_7_out, and_8_out, and_9_out, and_10_out, and_11_out,
       and_12_out, and_13_out, and_14_out, and_15_out, and_16_out, and_17_out, and_18_out, and_19_out,
       and_20_out, and_21_out, and_22_out, and_23_out, and_24_out, and_25_out, and_26_out, and_27_out,
       and_28_out, and_29_out, and_30_out, and_31_out, and_32_out, and_33_out, and_34_out, and_35_out,
       and_36_out, and_37_out, and_38_out, and_39_out, and_40_out, and_41_out, and_42_out, and_43_out,
       and_44_out, and_45_out, and_46_out, and_47_out, and_48_out, and_49_out, and_50_out, and_51_out,
       and_52_out, and_53_out, and_54_out, and_55_out, and_56_out, and_57_out, and_58_out, and_59_out,
       and_60_out, and_61_out, and_62_out, and_63_out, and_65_out, and_66_out, and_67_out, and_69_out,
       barrelshifter_1_out, full_adder_1_p3, full_adder_1_p4, full_adder_1_p5, full_adder_2_p3,
       full_adder_2_p5, full_adder_3_p3, full_adder_3_p5, full_adder_4_p3, full_adder_4_p4, full_adder_4_p5,
       full_adder_5_p3, full_adder_5_p5, full_adder_6_p3, full_adder_6_p5, full_adder_7_p3, full_adder_7_p5,
       full_adder_8_p3, full_adder_8_p5, full_adder_9_p3, full_adder_9_p5, full_adder_10_p3,
       full_adder_10_p5, full_adder_11_p3, full_adder_11_p5, full_adder_12_p3, full_adder_12_p5,
       full_adder_13_p3, full_adder_13_p5, full_adder_14_p3, full_adder_14_p5, full_adder_15_p3,
       full_adder_15_p5, full_adder_16_p3, full_adder_16_p5, full_adder_17_p3, full_adder_17_p5,
       full_adder_18_p3, full_adder_18_p5, full_adder_19_p3, full_adder_19_p5, full_adder_20_p3,
       full_adder_20_p5, full_adder_21_p3, full_adder_21_p5, full_adder_22_p3, full_adder_22_p5,
       full_adder_23_p3, full_adder_23_p5, full_adder_24_p3, full_adder_24_p5, full_adder_25_p3,
       full_adder_25_p5, full_adder_26_p3, full_adder_26_p5, full_adder_27_p3, full_adder_27_p5,
       full_adder_28_p3, full_adder_28_p5, full_adder_29_p3, full_adder_29_p5, full_adder_30_p3,
       full_adder_30_p5, full_adder_31_p3, full_adder_31_p5, full_adder_32_p3, full_adder_32_p5,
       full_adder_33_p3, full_adder_33_p5, full_adder_34_p3, full_adder_34_p5, full_adder_35_p3,
       full_adder_35_p5, full_adder_36_p3, full_adder_36_p5, full_adder_37_p3, full_adder_37_p5,
       full_adder_38_p3, full_adder_38_p5, full_adder_39_p3, full_adder_39_p5, full_adder_40_p3,
       full_adder_40_p5, full_adder_41_p3, full_adder_41_p5, full_adder_42_p3, full_adder_42_p5,
       full_adder_43_p3, full_adder_43_p5, full_adder_44_p3, full_adder_44_p5, full_adder_45_p3,
       full_adder_45_p5, full_adder_46_p3, full_adder_46_p5, full_adder_47_p3, full_adder_47_p5,
       full_adder_48_p3, full_adder_48_p5, full_adder_49_p3, full_adder_49_p5, full_adder_50_p3,
       full_adder_50_p5, full_adder_51_p3, full_adder_51_p5, full_adder_52_p3, full_adder_52_p5,
       full_adder_53_p3, full_adder_53_p5, full_adder_54_p3, full_adder_54_p5, full_adder_55_p3,
       full_adder_55_p5, full_adder_56_p3, full_adder_56_p5, full_adder_57_p3, full_adder_57_p5,
       full_adder_58_p3, full_adder_58_p5, full_adder_59_p3, full_adder_59_p5, full_adder_60_p3,
       full_adder_60_p5, full_adder_61_p3, full_adder_61_p5, full_adder_62_p3, full_adder_62_p5,
       full_adder_63_p3, full_adder_63_p5, full_adder_64_p3, full_adder_64_p5, multiplexer_1_out,
       multiplexer_3_out, multiplexer_6_out, multiplexer_7_out, multiplexer_8_out, multiplexer_9_out,
       multiplexer_12_out, multiplexer_13_out, multiplexer_16_out, multiplexer_17_out, multiplexer_18_out,
       multiplexer_20_out, multiplexer_21_out, multiplexer_24_out, multiplexer_25_out, multiplexer_28_out,
       multiplexer_29_out, multiplexer_32_out, multiplexer_33_out, multiplexer_36_out, multiplexer_37_out,
       multiplexer_40_out, multiplexer_41_out, multiplexer_44_out, multiplexer_45_out, multiplexer_48_out,
       multiplexer_49_out, multiplexer_52_out, multiplexer_53_out, multiplexer_56_out, multiplexer_57_out,
       multiplexer_60_out, multiplexer_61_out, multiplexer_64_out, multiplexer_65_out, multiplexer_68_out,
       multiplexer_69_out, multiplexer_72_out, multiplexer_73_out, multiplexer_76_out, multiplexer_77_out,
       multiplexer_80_out, multiplexer_81_out, multiplexer_84_out, multiplexer_85_out, multiplexer_88_out,
       multiplexer_89_out, multiplexer_92_out, multiplexer_93_out, multiplexer_96_out, multiplexer_97_out,
       multiplexer_100_out, multiplexer_101_out, multiplexer_104_out, multiplexer_105_out,
       multiplexer_108_out, multiplexer_109_out, multiplexer_112_out, multiplexer_113_out,
       multiplexer_116_out, multiplexer_117_out, multiplexer_120_out, multiplexer_121_out,
       multiplexer_124_out, multiplexer_126_out, multiplexer_128_out, not_1_out, not_2_out, not_3_out,
       not_4_out, not_5_out, not_6_out, not_7_out, not_8_out, not_9_out, not_10_out, not_11_out, not_12_out,
       not_13_out, not_14_out, not_15_out, not_16_out, not_17_out, not_18_out, not_19_out, not_20_out,
       not_21_out, not_22_out, not_23_out, not_24_out, not_25_out, not_26_out, not_27_out, not_28_out,
       not_29_out, not_30_out, not_31_out, not_32_out, not_33_out, not_34_out, not_35_out, not_36_out,
       not_37_out, not_38_out, not_39_out, not_40_out, not_41_out, not_42_out, not_43_out, not_44_out,
       not_45_out, not_46_out, not_47_out, not_48_out, not_49_out, not_50_out, not_51_out, not_52_out,
       not_53_out, not_54_out, not_55_out, not_56_out, not_57_out, not_58_out, not_59_out, not_60_out,
       not_61_out, not_62_out, not_63_out, not_64_out, not_65_out, not_66_out, not_67_out, not_68_out,
       not_69_out, or_1_out, or_2_out, or_3_out, or_4_out, or_5_out, or_6_out, or_7_out, or_8_out, or_9_out,
       or_10_out, or_11_out, or_12_out, or_13_out, or_14_out, or_15_out, or_16_out, or_17_out, or_18_out,
       or_19_out, or_20_out, or_21_out, or_22_out, or_23_out, or_24_out, or_25_out, or_26_out, or_27_out,
       or_28_out, or_29_out, or_30_out, or_31_out, or_32_out, or_33_out, or_34_out, or_35_out, or_36_out,
       or_37_out, or_38_out, or_39_out, or_40_out, or_41_out, or_42_out, or_43_out, or_44_out, or_45_out,
       or_46_out, or_47_out, or_48_out, or_49_out, or_50_out, or_51_out, or_52_out, or_53_out, or_54_out,
       or_55_out, or_56_out, or_57_out, or_58_out, or_59_out, or_60_out, or_61_out, or_62_out, or_63_out,
       or_64_out, xor_2_out, xor_4_out, xor_5_out, xor_6_out, xor_7_out, xor_8_out, xor_9_out, xor_10_out,
       xor_11_out, xor_12_out, xor_13_out, xor_14_out, xor_15_out, xor_16_out, xor_17_out, xor_18_out,
       xor_19_out, xor_20_out, xor_21_out, xor_22_out, xor_23_out, xor_24_out, xor_25_out, xor_26_out,
       xor_27_out, xor_28_out, xor_29_out, xor_30_out, xor_31_out, xor_32_out, xor_33_out, xor_34_out,
       xor_35_out, xor_36_out, xor_37_out, xor_38_out, xor_39_out, xor_40_out, xor_41_out, xor_42_out,
       xor_43_out, xor_44_out, xor_45_out, xor_46_out, xor_47_out, xor_48_out, xor_49_out, xor_50_out,
       xor_51_out, xor_52_out, xor_53_out, xor_54_out, xor_55_out, xor_56_out, xor_57_out, xor_58_out,
       xor_59_out, xor_60_out, xor_61_out, xor_62_out, xor_63_out, xor_64_out, xor_65_out, xor_66_out;
  wire [30:0] multiplexer_129_out;
  wire [31:0] barrelshifter_2_out;

  and and_1 (zero_2, ~neg_2, ~R_2[30], ~multiplexer_7_out, ~R_2[28], ~R_2[27], ~R_2[26], ~R_2[25], ~R_2[24], ~R_2[23], ~R_2[22], ~R_2[21], ~R_2[20], ~R_2[19], ~R_2[18], ~R_2[17], ~R_2[16], ~R_2[15], ~R_2[14], ~R_2[13], ~R_2[12], ~R_2[11], ~R_2[10], ~R_2[9], ~R_2[8], ~R_2[7], ~R_2[6], ~R_2[5], ~R_2[4], ~R_2[3], ~R_2[2], ~R_2[1], ~R_2[0]);  // And
  and and_2 (zero, ~neg, ~multiplexer_129_out[30], ~multiplexer_18_out, ~multiplexer_129_out[28], ~multiplexer_129_out[27], ~multiplexer_129_out[26], ~multiplexer_129_out[25], ~multiplexer_129_out[24], ~multiplexer_129_out[23], ~multiplexer_129_out[22], ~multiplexer_129_out[21], ~multiplexer_129_out[20], ~multiplexer_129_out[19], ~multiplexer_129_out[18], ~multiplexer_129_out[17], ~multiplexer_129_out[16], ~multiplexer_129_out[15], ~multiplexer_129_out[14], ~multiplexer_129_out[13], ~multiplexer_129_out[12], ~multiplexer_129_out[11], ~multiplexer_129_out[10], ~multiplexer_129_out[9], ~multiplexer_129_out[8], ~multiplexer_129_out[7], ~multiplexer_129_out[6], ~multiplexer_129_out[5], ~multiplexer_129_out[4], ~multiplexer_129_out[3], ~multiplexer_129_out[2], ~multiplexer_129_out[1], ~multiplexer_129_out[0]);  // And
  xor xor_1 (overflow_2, full_adder_1_p3, full_adder_1_p4);
  not not_1 (not_1_out, B_2[31]);
  Multiplexer multiplexer_1 (.sel(full_adder_61_p3), .in_0(B_2[31]), .in_1(not_1_out), .out(multiplexer_1_out));
  and and_3 (and_3_out, B_2[31], A_2[31]);
  // full_adder full_adder_1: pin names not known; wires that end beside it: A_2[31], multiplexer_1_out, full_adder_1_p3, full_adder_1_p4, full_adder_1_p5
  or or_1 (or_1_out, B_2[31], A_2[31]);
  xor xor_2 (xor_2_out, B_2[31], A_2[31]);
  Multiplexer #(.Selector_Bits(3)) multiplexer_2 (
    .sel(F_2), .in_0(full_adder_1_p5), .in_1(full_adder_1_p5), .in_2(xor_2_out), .in_3(or_1_out),
    .in_4(and_3_out), .in_5(barrelshifter_1_out), .in_6(barrelshifter_1_out), .in_7(barrelshifter_1_out),
    .out(neg_2));
  not not_2 (not_2_out, B_2[30]);
  Multiplexer multiplexer_3 (.sel(full_adder_61_p3), .in_0(B_2[30]), .in_1(not_2_out), .out(multiplexer_3_out));
  and and_4 (and_4_out, B_2[30], A_2[30]);
  // full_adder full_adder_2: pin names not known; wires that end beside it: A_2[30], multiplexer_3_out, full_adder_2_p3, full_adder_1_p3, full_adder_2_p5
  or or_2 (or_2_out, B_2[30], A_2[30]);
  xor xor_3 (overflow, full_adder_4_p3, full_adder_4_p4);
  xor xor_4 (xor_4_out, B_2[30], A_2[30]);
  Multiplexer #(.Selector_Bits(3)) multiplexer_4 (
    .sel(F_2), .in_0(full_adder_2_p5), .in_1(full_adder_2_p5), .in_2(xor_4_out), .in_3(or_2_out),
    .in_4(and_4_out), .in_5(barrelshifter_1_out), .in_6(barrelshifter_1_out), .in_7(barrelshifter_1_out),
    .out(R_2[30]));
  Multiplexer #(.Bits(32)) multiplexer_5 (
    .sel(and_69_out), .in_0({neg, {2{multiplexer_129_out[30]}}, multiplexer_129_out[28:0]}),
    .in_1(barrelshifter_2_out), .out(R));
  not not_3 (not_3_out, B_2[29]);
  Multiplexer multiplexer_6 (.sel(full_adder_61_p3), .in_0(B_2[29]), .in_1(not_3_out), .out(multiplexer_6_out));
  and and_5 (and_5_out, B_2[29], A_2[29]);
  // full_adder full_adder_3: pin names not known; wires that end beside it: A_2[29], multiplexer_6_out, full_adder_3_p3, full_adder_2_p3, full_adder_3_p5
  or or_3 (or_3_out, B_2[29], A_2[29]);
  xor xor_5 (xor_5_out, B_2[29], A_2[29]);
  Multiplexer #(.Selector_Bits(3)) multiplexer_7 (
    .sel(F_2), .in_0(full_adder_3_p5), .in_1(full_adder_3_p5), .in_2(xor_5_out), .in_3(or_3_out),
    .in_4(and_5_out), .in_5(barrelshifter_1_out), .in_6(barrelshifter_1_out), .in_7(barrelshifter_1_out),
    .out(multiplexer_7_out));
  not not_4 (not_4_out, B[31]);
  and and_6 (and_6_out, B[31], A[31]);
  Multiplexer multiplexer_8 (.sel(full_adder_64_p3), .in_0(B[31]), .in_1(not_4_out), .out(multiplexer_8_out));
  // full_adder full_adder_4: pin names not known; wires that end beside it: A[31], multiplexer_8_out, full_adder_4_p3, full_adder_4_p4, full_adder_4_p5
  or or_4 (or_4_out, B[31], A[31]);
  not not_5 (not_5_out, B_2[28]);
  Multiplexer multiplexer_9 (.sel(full_adder_61_p3), .in_0(B_2[28]), .in_1(not_5_out), .out(multiplexer_9_out));
  and and_7 (and_7_out, B_2[28], A_2[28]);
  xor xor_6 (xor_6_out, B[31], A[31]);
  // full_adder full_adder_5: pin names not known; wires that end beside it: A_2[28], multiplexer_9_out, full_adder_5_p3, full_adder_3_p3, full_adder_5_p5
  or or_5 (or_5_out, B_2[28], A_2[28]);
  Multiplexer #(.Selector_Bits(3)) multiplexer_10 (
    .sel(F), .in_0(full_adder_4_p5), .in_1(full_adder_4_p5), .in_2(xor_6_out), .in_3(or_4_out),
    .in_4(and_6_out), .in_5(1'b0), .in_6(1'b0), .in_7(1'b0), .out(neg));
  xor xor_7 (xor_7_out, B_2[28], A_2[28]);
  Multiplexer #(.Selector_Bits(3)) multiplexer_11 (
    .sel(F_2), .in_0(full_adder_5_p5), .in_1(full_adder_5_p5), .in_2(xor_7_out), .in_3(or_5_out),
    .in_4(and_7_out), .in_5(barrelshifter_1_out), .in_6(barrelshifter_1_out), .in_7(barrelshifter_1_out),
    .out(R_2[28]));
  not not_6 (not_6_out, B[30]);
  Multiplexer multiplexer_12 (.sel(full_adder_64_p3), .in_0(B[30]), .in_1(not_6_out), .out(multiplexer_12_out));
  and and_8 (and_8_out, B[30], A[30]);
  not not_7 (not_7_out, B_2[27]);
  // full_adder full_adder_6: pin names not known; wires that end beside it: A[30], multiplexer_12_out, full_adder_6_p3, full_adder_4_p3, full_adder_6_p5
  or or_6 (or_6_out, B[30], A[30]);
  Multiplexer multiplexer_13 (.sel(full_adder_61_p3), .in_0(B_2[27]), .in_1(not_7_out), .out(multiplexer_13_out));
  and and_9 (and_9_out, B_2[27], A_2[27]);
  xor xor_8 (xor_8_out, B[30], A[30]);
  Multiplexer #(.Selector_Bits(3)) multiplexer_14 (
    .sel(F), .in_0(full_adder_6_p5), .in_1(full_adder_6_p5), .in_2(xor_8_out), .in_3(or_6_out),
    .in_4(and_8_out), .in_5(1'b0), .in_6(1'b0), .in_7(1'b0), .out(multiplexer_129_out[30]));
  // full_adder full_adder_7: pin names not known; wires that end beside it: A_2[27], multiplexer_13_out, full_adder_7_p3, full_adder_5_p3, full_adder_7_p5
  or or_7 (or_7_out, B_2[27], A_2[27]);
  xor xor_9 (xor_9_out, B_2[27], A_2[27]);
  Multiplexer #(.Selector_Bits(3)) multiplexer_15 (
    .sel(F_2), .in_0(full_adder_7_p5), .in_1(full_adder_7_p5), .in_2(xor_9_out), .in_3(or_7_out),
    .in_4(and_9_out), .in_5(barrelshifter_1_out), .in_6(barrelshifter_1_out), .in_7(barrelshifter_1_out),
    .out(R_2[27]));
  not not_8 (not_8_out, B[29]);
  and and_10 (and_10_out, B[29], A[29]);
  Multiplexer multiplexer_16 (.sel(full_adder_64_p3), .in_0(B[29]), .in_1(not_8_out), .out(multiplexer_16_out));
  // full_adder full_adder_8: pin names not known; wires that end beside it: A[29], multiplexer_16_out, full_adder_8_p3, full_adder_6_p3, full_adder_8_p5
  or or_8 (or_8_out, B[29], A[29]);
  not not_9 (not_9_out, B_2[26]);
  Multiplexer multiplexer_17 (.sel(full_adder_61_p3), .in_0(B_2[26]), .in_1(not_9_out), .out(multiplexer_17_out));
  and and_11 (and_11_out, B_2[26], A_2[26]);
  xor xor_10 (xor_10_out, B[29], A[29]);
  // full_adder full_adder_9: pin names not known; wires that end beside it: A_2[26], multiplexer_17_out, full_adder_9_p3, full_adder_7_p3, full_adder_9_p5
  or or_9 (or_9_out, B_2[26], A_2[26]);
  Multiplexer #(.Selector_Bits(3)) multiplexer_18 (
    .sel(F), .in_0(full_adder_8_p5), .in_1(full_adder_8_p5), .in_2(xor_10_out), .in_3(or_8_out),
    .in_4(and_10_out), .in_5(1'b0), .in_6(1'b0), .in_7(1'b0), .out(multiplexer_18_out));
  xor xor_11 (xor_11_out, B_2[26], A_2[26]);
  Multiplexer #(.Selector_Bits(3)) multiplexer_19 (
    .sel(F_2), .in_0(full_adder_9_p5), .in_1(full_adder_9_p5), .in_2(xor_11_out), .in_3(or_9_out),
    .in_4(and_11_out), .in_5(barrelshifter_1_out), .in_6(barrelshifter_1_out), .in_7(barrelshifter_1_out),
    .out(R_2[26]));
  not not_10 (not_10_out, B[28]);
  Multiplexer multiplexer_20 (.sel(full_adder_64_p3), .in_0(B[28]), .in_1(not_10_out), .out(multiplexer_20_out));
  and and_12 (and_12_out, B[28], A[28]);
  not not_11 (not_11_out, B_2[25]);
  // full_adder full_adder_10: pin names not known; wires that end beside it: A[28], multiplexer_20_out, full_adder_10_p3, full_adder_8_p3, full_adder_10_p5
  or or_10 (or_10_out, B[28], A[28]);
  Multiplexer multiplexer_21 (.sel(full_adder_61_p3), .in_0(B_2[25]), .in_1(not_11_out), .out(multiplexer_21_out));
  and and_13 (and_13_out, B_2[25], A_2[25]);
  xor xor_12 (xor_12_out, B[28], A[28]);
  Multiplexer #(.Selector_Bits(3)) multiplexer_22 (
    .sel(F), .in_0(full_adder_10_p5), .in_1(full_adder_10_p5), .in_2(xor_12_out), .in_3(or_10_out),
    .in_4(and_12_out), .in_5(1'b0), .in_6(1'b0), .in_7(1'b0), .out(multiplexer_129_out[28]));
  // full_adder full_adder_11: pin names not known; wires that end beside it: A_2[25], multiplexer_21_out, full_adder_11_p3, full_adder_9_p3, full_adder_11_p5
  or or_11 (or_11_out, B_2[25], A_2[25]);
  xor xor_13 (xor_13_out, B_2[25], A_2[25]);
  Multiplexer #(.Selector_Bits(3)) multiplexer_23 (
    .sel(F_2), .in_0(full_adder_11_p5), .in_1(full_adder_11_p5), .in_2(xor_13_out), .in_3(or_11_out),
    .in_4(and_13_out), .in_5(barrelshifter_1_out), .in_6(barrelshifter_1_out), .in_7(barrelshifter_1_out),
    .out(R_2[25]));
  not not_12 (not_12_out, B[27]);
  and and_14 (and_14_out, B[27], A[27]);
  Multiplexer multiplexer_24 (.sel(full_adder_64_p3), .in_0(B[27]), .in_1(not_12_out), .out(multiplexer_24_out));
  // full_adder full_adder_12: pin names not known; wires that end beside it: A[27], multiplexer_24_out, full_adder_12_p3, full_adder_10_p3, full_adder_12_p5
  or or_12 (or_12_out, B[27], A[27]);
  not not_13 (not_13_out, B_2[24]);
  Multiplexer multiplexer_25 (.sel(full_adder_61_p3), .in_0(B_2[24]), .in_1(not_13_out), .out(multiplexer_25_out));
  and and_15 (and_15_out, B_2[24], A_2[24]);
  xor xor_14 (xor_14_out, B[27], A[27]);
  // full_adder full_adder_13: pin names not known; wires that end beside it: A_2[24], multiplexer_25_out, full_adder_13_p3, full_adder_11_p3, full_adder_13_p5
  or or_13 (or_13_out, B_2[24], A_2[24]);
  Multiplexer #(.Selector_Bits(3)) multiplexer_26 (
    .sel(F), .in_0(full_adder_12_p5), .in_1(full_adder_12_p5), .in_2(xor_14_out), .in_3(or_12_out),
    .in_4(and_14_out), .in_5(1'b0), .in_6(1'b0), .in_7(1'b0), .out(multiplexer_129_out[27]));
  xor xor_15 (xor_15_out, B_2[24], A_2[24]);
  Multiplexer #(.Selector_Bits(3)) multiplexer_27 (
    .sel(F_2), .in_0(full_adder_13_p5), .in_1(full_adder_13_p5), .in_2(xor_15_out), .in_3(or_13_out),
    .in_4(and_15_out), .in_5(barrelshifter_1_out), .in_6(barrelshifter_1_out), .in_7(barrelshifter_1_out),
    .out(R_2[24]));
  not not_14 (not_14_out, B[26]);
  Multiplexer multiplexer_28 (.sel(full_adder_64_p3), .in_0(B[26]), .in_1(not_14_out), .out(multiplexer_28_out));
  and and_16 (and_16_out, B[26], A[26]);
  not not_15 (not_15_out, B_2[23]);
  // full_adder full_adder_14: pin names not known; wires that end beside it: A[26], multiplexer_28_out, full_adder_14_p3, full_adder_12_p3, full_adder_14_p5
  or or_14 (or_14_out, B[26], A[26]);
  Multiplexer multiplexer_29 (.sel(full_adder_61_p3), .in_0(B_2[23]), .in_1(not_15_out), .out(multiplexer_29_out));
  and and_17 (and_17_out, B_2[23], A_2[23]);
  xor xor_16 (xor_16_out, B[26], A[26]);
  Multiplexer #(.Selector_Bits(3)) multiplexer_30 (
    .sel(F), .in_0(full_adder_14_p5), .in_1(full_adder_14_p5), .in_2(xor_16_out), .in_3(or_14_out),
    .in_4(and_16_out), .in_5(1'b0), .in_6(1'b0), .in_7(1'b0), .out(multiplexer_129_out[26]));
  // full_adder full_adder_15: pin names not known; wires that end beside it: A_2[23], multiplexer_29_out, full_adder_15_p3, full_adder_13_p3, full_adder_15_p5
  or or_15 (or_15_out, B_2[23], A_2[23]);
  xor xor_17 (xor_17_out, B_2[23], A_2[23]);
  Multiplexer #(.Selector_Bits(3)) multiplexer_31 (
    .sel(F_2), .in_0(full_adder_15_p5), .in_1(full_adder_15_p5), .in_2(xor_17_out), .in_3(or_15_out),
    .in_4(and_17_out), .in_5(barrelshifter_1_out), .in_6(barrelshifter_1_out), .in_7(barrelshifter_1_out),
    .out(R_2[23]));
  not not_16 (not_16_out, B[25]);
  and and_18 (and_18_out, B[25], A[25]);
  Multiplexer multiplexer_32 (.sel(full_adder_64_p3), .in_0(B[25]), .in_1(not_16_out), .out(multiplexer_32_out));
  // full_adder full_adder_16: pin names not known; wires that end beside it: A[25], multiplexer_32_out, full_adder_16_p3, full_adder_14_p3, full_adder_16_p5
  or or_16 (or_16_out, B[25], A[25]);
  not not_17 (not_17_out, B_2[22]);
  Multiplexer multiplexer_33 (.sel(full_adder_61_p3), .in_0(B_2[22]), .in_1(not_17_out), .out(multiplexer_33_out));
  and and_19 (and_19_out, B_2[22], A_2[22]);
  xor xor_18 (xor_18_out, B[25], A[25]);
  // full_adder full_adder_17: pin names not known; wires that end beside it: A_2[22], multiplexer_33_out, full_adder_17_p3, full_adder_15_p3, full_adder_17_p5
  or or_17 (or_17_out, B_2[22], A_2[22]);
  Multiplexer #(.Selector_Bits(3)) multiplexer_34 (
    .sel(F), .in_0(full_adder_16_p5), .in_1(full_adder_16_p5), .in_2(xor_18_out), .in_3(or_16_out),
    .in_4(and_18_out), .in_5(1'b0), .in_6(1'b0), .in_7(1'b0), .out(multiplexer_129_out[25]));
  xor xor_19 (xor_19_out, B_2[22], A_2[22]);
  Multiplexer #(.Selector_Bits(3)) multiplexer_35 (
    .sel(F_2), .in_0(full_adder_17_p5), .in_1(full_adder_17_p5), .in_2(xor_19_out), .in_3(or_17_out),
    .in_4(and_19_out), .in_5(barrelshifter_1_out), .in_6(barrelshifter_1_out), .in_7(barrelshifter_1_out),
    .out(R_2[22]));
  not not_18 (not_18_out, B[24]);
  Multiplexer multiplexer_36 (.sel(full_adder_64_p3), .in_0(B[24]), .in_1(not_18_out), .out(multiplexer_36_out));
  and and_20 (and_20_out, B[24], A[24]);
  not not_19 (not_19_out, B_2[21]);
  // full_adder full_adder_18: pin names not known; wires that end beside it: A[24], multiplexer_36_out, full_adder_18_p3, full_adder_16_p3, full_adder_18_p5
  or or_18 (or_18_out, B[24], A[24]);
  Multiplexer multiplexer_37 (.sel(full_adder_61_p3), .in_0(B_2[21]), .in_1(not_19_out), .out(multiplexer_37_out));
  and and_21 (and_21_out, B_2[21], A_2[21]);
  xor xor_20 (xor_20_out, B[24], A[24]);
  Multiplexer #(.Selector_Bits(3)) multiplexer_38 (
    .sel(F), .in_0(full_adder_18_p5), .in_1(full_adder_18_p5), .in_2(xor_20_out), .in_3(or_18_out),
    .in_4(and_20_out), .in_5(1'b0), .in_6(1'b0), .in_7(1'b0), .out(multiplexer_129_out[24]));
  // full_adder full_adder_19: pin names not known; wires that end beside it: A_2[21], multiplexer_37_out, full_adder_19_p3, full_adder_17_p3, full_adder_19_p5
  or or_19 (or_19_out, B_2[21], A_2[21]);
  xor xor_21 (xor_21_out, B_2[21], A_2[21]);
  Multiplexer #(.Selector_Bits(3)) multiplexer_39 (
    .sel(F_2), .in_0(full_adder_19_p5), .in_1(full_adder_19_p5), .in_2(xor_21_out), .in_3(or_19_out),
    .in_4(and_21_out), .in_5(barrelshifter_1_out), .in_6(barrelshifter_1_out), .in_7(barrelshifter_1_out),
    .out(R_2[21]));
  not not_20 (not_20_out, B[23]);
  and and_22 (and_22_out, B[23], A[23]);
  Multiplexer multiplexer_40 (.sel(full_adder_64_p3), .in_0(B[23]), .in_1(not_20_out), .out(multiplexer_40_out));
  // full_adder full_adder_20: pin names not known; wires that end beside it: A[23], multiplexer_40_out, full_adder_20_p3, full_adder_18_p3, full_adder_20_p5
  or or_20 (or_20_out, B[23], A[23]);
  not not_21 (not_21_out, B_2[20]);
  Multiplexer multiplexer_41 (.sel(full_adder_61_p3), .in_0(B_2[20]), .in_1(not_21_out), .out(multiplexer_41_out));
  and and_23 (and_23_out, B_2[20], A_2[20]);
  xor xor_22 (xor_22_out, B[23], A[23]);
  // full_adder full_adder_21: pin names not known; wires that end beside it: A_2[20], multiplexer_41_out, full_adder_21_p3, full_adder_19_p3, full_adder_21_p5
  or or_21 (or_21_out, B_2[20], A_2[20]);
  Multiplexer #(.Selector_Bits(3)) multiplexer_42 (
    .sel(F), .in_0(full_adder_20_p5), .in_1(full_adder_20_p5), .in_2(xor_22_out), .in_3(or_20_out),
    .in_4(and_22_out), .in_5(1'b0), .in_6(1'b0), .in_7(1'b0), .out(multiplexer_129_out[23]));
  xor xor_23 (xor_23_out, B_2[20], A_2[20]);
  Multiplexer #(.Selector_Bits(3)) multiplexer_43 (
    .sel(F_2), .in_0(full_adder_21_p5), .in_1(full_adder_21_p5), .in_2(xor_23_out), .in_3(or_21_out),
    .in_4(and_23_out), .in_5(barrelshifter_1_out), .in_6(barrelshifter_1_out), .in_7(barrelshifter_1_out),
    .out(R_2[20]));
  not not_22 (not_22_out, B[22]);
  Multiplexer multiplexer_44 (.sel(full_adder_64_p3), .in_0(B[22]), .in_1(not_22_out), .out(multiplexer_44_out));
  and and_24 (and_24_out, B[22], A[22]);
  not not_23 (not_23_out, B_2[19]);
  // full_adder full_adder_22: pin names not known; wires that end beside it: A[22], multiplexer_44_out, full_adder_22_p3, full_adder_20_p3, full_adder_22_p5
  or or_22 (or_22_out, B[22], A[22]);
  Multiplexer multiplexer_45 (.sel(full_adder_61_p3), .in_0(B_2[19]), .in_1(not_23_out), .out(multiplexer_45_out));
  and and_25 (and_25_out, B_2[19], A_2[19]);
  xor xor_24 (xor_24_out, B[22], A[22]);
  Multiplexer #(.Selector_Bits(3)) multiplexer_46 (
    .sel(F), .in_0(full_adder_22_p5), .in_1(full_adder_22_p5), .in_2(xor_24_out), .in_3(or_22_out),
    .in_4(and_24_out), .in_5(1'b0), .in_6(1'b0), .in_7(1'b0), .out(multiplexer_129_out[22]));
  // full_adder full_adder_23: pin names not known; wires that end beside it: A_2[19], multiplexer_45_out, full_adder_23_p3, full_adder_21_p3, full_adder_23_p5
  or or_23 (or_23_out, B_2[19], A_2[19]);
  xor xor_25 (xor_25_out, B_2[19], A_2[19]);
  Multiplexer #(.Selector_Bits(3)) multiplexer_47 (
    .sel(F_2), .in_0(full_adder_23_p5), .in_1(full_adder_23_p5), .in_2(xor_25_out), .in_3(or_23_out),
    .in_4(and_25_out), .in_5(barrelshifter_1_out), .in_6(barrelshifter_1_out), .in_7(barrelshifter_1_out),
    .out(R_2[19]));
  not not_24 (not_24_out, B[21]);
  and and_26 (and_26_out, B[21], A[21]);
  Multiplexer multiplexer_48 (.sel(full_adder_64_p3), .in_0(B[21]), .in_1(not_24_out), .out(multiplexer_48_out));
  // full_adder full_adder_24: pin names not known; wires that end beside it: A[21], multiplexer_48_out, full_adder_24_p3, full_adder_22_p3, full_adder_24_p5
  or or_24 (or_24_out, B[21], A[21]);
  not not_25 (not_25_out, B_2[18]);
  Multiplexer multiplexer_49 (.sel(full_adder_61_p3), .in_0(B_2[18]), .in_1(not_25_out), .out(multiplexer_49_out));
  and and_27 (and_27_out, B_2[18], A_2[18]);
  xor xor_26 (xor_26_out, B[21], A[21]);
  // full_adder full_adder_25: pin names not known; wires that end beside it: A_2[18], multiplexer_49_out, full_adder_25_p3, full_adder_23_p3, full_adder_25_p5
  or or_25 (or_25_out, B_2[18], A_2[18]);
  Multiplexer #(.Selector_Bits(3)) multiplexer_50 (
    .sel(F), .in_0(full_adder_24_p5), .in_1(full_adder_24_p5), .in_2(xor_26_out), .in_3(or_24_out),
    .in_4(and_26_out), .in_5(1'b0), .in_6(1'b0), .in_7(1'b0), .out(multiplexer_129_out[21]));
  xor xor_27 (xor_27_out, B_2[18], A_2[18]);
  Multiplexer #(.Selector_Bits(3)) multiplexer_51 (
    .sel(F_2), .in_0(full_adder_25_p5), .in_1(full_adder_25_p5), .in_2(xor_27_out), .in_3(or_25_out),
    .in_4(and_27_out), .in_5(barrelshifter_1_out), .in_6(barrelshifter_1_out), .in_7(barrelshifter_1_out),
    .out(R_2[18]));
  not not_26 (not_26_out, B[20]);
  Multiplexer multiplexer_52 (.sel(full_adder_64_p3), .in_0(B[20]), .in_1(not_26_out), .out(multiplexer_52_out));
  and and_28 (and_28_out, B[20], A[20]);
  not not_27 (not_27_out, B_2[17]);
  // full_adder full_adder_26: pin names not known; wires that end beside it: A[20], multiplexer_52_out, full_adder_26_p3, full_adder_24_p3, full_adder_26_p5
  or or_26 (or_26_out, B[20], A[20]);
  Multiplexer multiplexer_53 (.sel(full_adder_61_p3), .in_0(B_2[17]), .in_1(not_27_out), .out(multiplexer_53_out));
  and and_29 (and_29_out, B_2[17], A_2[17]);
  xor xor_28 (xor_28_out, B[20], A[20]);
  Multiplexer #(.Selector_Bits(3)) multiplexer_54 (
    .sel(F), .in_0(full_adder_26_p5), .in_1(full_adder_26_p5), .in_2(xor_28_out), .in_3(or_26_out),
    .in_4(and_28_out), .in_5(1'b0), .in_6(1'b0), .in_7(1'b0), .out(multiplexer_129_out[20]));
  // full_adder full_adder_27: pin names not known; wires that end beside it: A_2[17], multiplexer_53_out, full_adder_27_p3, full_adder_25_p3, full_adder_27_p5
  or or_27 (or_27_out, B_2[17], A_2[17]);
  xor xor_29 (xor_29_out, B_2[17], A_2[17]);
  Multiplexer #(.Selector_Bits(3)) multiplexer_55 (
    .sel(F_2), .in_0(full_adder_27_p5), .in_1(full_adder_27_p5), .in_2(xor_29_out), .in_3(or_27_out),
    .in_4(and_29_out), .in_5(barrelshifter_1_out), .in_6(barrelshifter_1_out), .in_7(barrelshifter_1_out),
    .out(R_2[17]));
  not not_28 (not_28_out, B[19]);
  and and_30 (and_30_out, B[19], A[19]);
  Multiplexer multiplexer_56 (.sel(full_adder_64_p3), .in_0(B[19]), .in_1(not_28_out), .out(multiplexer_56_out));
  // full_adder full_adder_28: pin names not known; wires that end beside it: A[19], multiplexer_56_out, full_adder_28_p3, full_adder_26_p3, full_adder_28_p5
  or or_28 (or_28_out, B[19], A[19]);
  not not_29 (not_29_out, B_2[16]);
  Multiplexer multiplexer_57 (.sel(full_adder_61_p3), .in_0(B_2[16]), .in_1(not_29_out), .out(multiplexer_57_out));
  and and_31 (and_31_out, B_2[16], A_2[16]);
  xor xor_30 (xor_30_out, B[19], A[19]);
  // full_adder full_adder_29: pin names not known; wires that end beside it: A_2[16], multiplexer_57_out, full_adder_29_p3, full_adder_27_p3, full_adder_29_p5
  or or_29 (or_29_out, B_2[16], A_2[16]);
  Multiplexer #(.Selector_Bits(3)) multiplexer_58 (
    .sel(F), .in_0(full_adder_28_p5), .in_1(full_adder_28_p5), .in_2(xor_30_out), .in_3(or_28_out),
    .in_4(and_30_out), .in_5(1'b0), .in_6(1'b0), .in_7(1'b0), .out(multiplexer_129_out[19]));
  xor xor_31 (xor_31_out, B_2[16], A_2[16]);
  Multiplexer #(.Selector_Bits(3)) multiplexer_59 (
    .sel(F_2), .in_0(full_adder_29_p5), .in_1(full_adder_29_p5), .in_2(xor_31_out), .in_3(or_29_out),
    .in_4(and_31_out), .in_5(barrelshifter_1_out), .in_6(barrelshifter_1_out), .in_7(barrelshifter_1_out),
    .out(R_2[16]));
  not not_30 (not_30_out, B[18]);
  Multiplexer multiplexer_60 (.sel(full_adder_64_p3), .in_0(B[18]), .in_1(not_30_out), .out(multiplexer_60_out));
  and and_32 (and_32_out, B[18], A[18]);
  not not_31 (not_31_out, B_2[15]);
  // full_adder full_adder_30: pin names not known; wires that end beside it: A[18], multiplexer_60_out, full_adder_30_p3, full_adder_28_p3, full_adder_30_p5
  or or_30 (or_30_out, B[18], A[18]);
  Multiplexer multiplexer_61 (.sel(full_adder_61_p3), .in_0(B_2[15]), .in_1(not_31_out), .out(multiplexer_61_out));
  and and_33 (and_33_out, B_2[15], A_2[15]);
  xor xor_32 (xor_32_out, B[18], A[18]);
  Multiplexer #(.Selector_Bits(3)) multiplexer_62 (
    .sel(F), .in_0(full_adder_30_p5), .in_1(full_adder_30_p5), .in_2(xor_32_out), .in_3(or_30_out),
    .in_4(and_32_out), .in_5(1'b0), .in_6(1'b0), .in_7(1'b0), .out(multiplexer_129_out[18]));
  // full_adder full_adder_31: pin names not known; wires that end beside it: A_2[15], multiplexer_61_out, full_adder_31_p3, full_adder_29_p3, full_adder_31_p5
  or or_31 (or_31_out, B_2[15], A_2[15]);
  xor xor_33 (xor_33_out, B_2[15], A_2[15]);
  Multiplexer #(.Selector_Bits(3)) multiplexer_63 (
    .sel(F_2), .in_0(full_adder_31_p5), .in_1(full_adder_31_p5), .in_2(xor_33_out), .in_3(or_31_out),
    .in_4(and_33_out), .in_5(barrelshifter_1_out), .in_6(barrelshifter_1_out), .in_7(barrelshifter_1_out),
    .out(R_2[15]));
  not not_32 (not_32_out, B[17]);
  and and_34 (and_34_out, B[17], A[17]);
  Multiplexer multiplexer_64 (.sel(full_adder_64_p3), .in_0(B[17]), .in_1(not_32_out), .out(multiplexer_64_out));
  // full_adder full_adder_32: pin names not known; wires that end beside it: A[17], multiplexer_64_out, full_adder_32_p3, full_adder_30_p3, full_adder_32_p5
  or or_32 (or_32_out, B[17], A[17]);
  not not_33 (not_33_out, B_2[14]);
  Multiplexer multiplexer_65 (.sel(full_adder_61_p3), .in_0(B_2[14]), .in_1(not_33_out), .out(multiplexer_65_out));
  and and_35 (and_35_out, B_2[14], A_2[14]);
  xor xor_34 (xor_34_out, B[17], A[17]);
  // full_adder full_adder_33: pin names not known; wires that end beside it: A_2[14], multiplexer_65_out, full_adder_33_p3, full_adder_31_p3, full_adder_33_p5
  or or_33 (or_33_out, B_2[14], A_2[14]);
  Multiplexer #(.Selector_Bits(3)) multiplexer_66 (
    .sel(F), .in_0(full_adder_32_p5), .in_1(full_adder_32_p5), .in_2(xor_34_out), .in_3(or_32_out),
    .in_4(and_34_out), .in_5(1'b0), .in_6(1'b0), .in_7(1'b0), .out(multiplexer_129_out[17]));
  xor xor_35 (xor_35_out, B_2[14], A_2[14]);
  Multiplexer #(.Selector_Bits(3)) multiplexer_67 (
    .sel(F_2), .in_0(full_adder_33_p5), .in_1(full_adder_33_p5), .in_2(xor_35_out), .in_3(or_33_out),
    .in_4(and_35_out), .in_5(barrelshifter_1_out), .in_6(barrelshifter_1_out), .in_7(barrelshifter_1_out),
    .out(R_2[14]));
  not not_34 (not_34_out, B[16]);
  Multiplexer multiplexer_68 (.sel(full_adder_64_p3), .in_0(B[16]), .in_1(not_34_out), .out(multiplexer_68_out));
  and and_36 (and_36_out, B[16], A[16]);
  not not_35 (not_35_out, B_2[13]);
  // full_adder full_adder_34: pin names not known; wires that end beside it: A[16], multiplexer_68_out, full_adder_34_p3, full_adder_32_p3, full_adder_34_p5
  or or_34 (or_34_out, B[16], A[16]);
  Multiplexer multiplexer_69 (.sel(full_adder_61_p3), .in_0(B_2[13]), .in_1(not_35_out), .out(multiplexer_69_out));
  and and_37 (and_37_out, B_2[13], A_2[13]);
  xor xor_36 (xor_36_out, B[16], A[16]);
  Multiplexer #(.Selector_Bits(3)) multiplexer_70 (
    .sel(F), .in_0(full_adder_34_p5), .in_1(full_adder_34_p5), .in_2(xor_36_out), .in_3(or_34_out),
    .in_4(and_36_out), .in_5(1'b0), .in_6(1'b0), .in_7(1'b0), .out(multiplexer_129_out[16]));
  // full_adder full_adder_35: pin names not known; wires that end beside it: A_2[13], multiplexer_69_out, full_adder_35_p3, full_adder_33_p3, full_adder_35_p5
  or or_35 (or_35_out, B_2[13], A_2[13]);
  xor xor_37 (xor_37_out, B_2[13], A_2[13]);
  Multiplexer #(.Selector_Bits(3)) multiplexer_71 (
    .sel(F_2), .in_0(full_adder_35_p5), .in_1(full_adder_35_p5), .in_2(xor_37_out), .in_3(or_35_out),
    .in_4(and_37_out), .in_5(barrelshifter_1_out), .in_6(barrelshifter_1_out), .in_7(barrelshifter_1_out),
    .out(R_2[13]));
  not not_36 (not_36_out, B[15]);
  and and_38 (and_38_out, B[15], A[15]);
  Multiplexer multiplexer_72 (.sel(full_adder_64_p3), .in_0(B[15]), .in_1(not_36_out), .out(multiplexer_72_out));
  // full_adder full_adder_36: pin names not known; wires that end beside it: A[15], multiplexer_72_out, full_adder_36_p3, full_adder_34_p3, full_adder_36_p5
  or or_36 (or_36_out, B[15], A[15]);
  not not_37 (not_37_out, B_2[12]);
  Multiplexer multiplexer_73 (.sel(full_adder_61_p3), .in_0(B_2[12]), .in_1(not_37_out), .out(multiplexer_73_out));
  and and_39 (and_39_out, B_2[12], A_2[12]);
  xor xor_38 (xor_38_out, B[15], A[15]);
  // full_adder full_adder_37: pin names not known; wires that end beside it: A_2[12], multiplexer_73_out, full_adder_37_p3, full_adder_35_p3, full_adder_37_p5
  or or_37 (or_37_out, B_2[12], A_2[12]);
  Multiplexer #(.Selector_Bits(3)) multiplexer_74 (
    .sel(F), .in_0(full_adder_36_p5), .in_1(full_adder_36_p5), .in_2(xor_38_out), .in_3(or_36_out),
    .in_4(and_38_out), .in_5(1'b0), .in_6(1'b0), .in_7(1'b0), .out(multiplexer_129_out[15]));
  xor xor_39 (xor_39_out, B_2[12], A_2[12]);
  Multiplexer #(.Selector_Bits(3)) multiplexer_75 (
    .sel(F_2), .in_0(full_adder_37_p5), .in_1(full_adder_37_p5), .in_2(xor_39_out), .in_3(or_37_out),
    .in_4(and_39_out), .in_5(barrelshifter_1_out), .in_6(barrelshifter_1_out), .in_7(barrelshifter_1_out),
    .out(R_2[12]));
  not not_38 (not_38_out, B[14]);
  Multiplexer multiplexer_76 (.sel(full_adder_64_p3), .in_0(B[14]), .in_1(not_38_out), .out(multiplexer_76_out));
  and and_40 (and_40_out, B[14], A[14]);
  not not_39 (not_39_out, B_2[11]);
  // full_adder full_adder_38: pin names not known; wires that end beside it: A[14], multiplexer_76_out, full_adder_38_p3, full_adder_36_p3, full_adder_38_p5
  or or_38 (or_38_out, B[14], A[14]);
  Multiplexer multiplexer_77 (.sel(full_adder_61_p3), .in_0(B_2[11]), .in_1(not_39_out), .out(multiplexer_77_out));
  and and_41 (and_41_out, B_2[11], A_2[11]);
  xor xor_40 (xor_40_out, B[14], A[14]);
  Multiplexer #(.Selector_Bits(3)) multiplexer_78 (
    .sel(F), .in_0(full_adder_38_p5), .in_1(full_adder_38_p5), .in_2(xor_40_out), .in_3(or_38_out),
    .in_4(and_40_out), .in_5(1'b0), .in_6(1'b0), .in_7(1'b0), .out(multiplexer_129_out[14]));
  // full_adder full_adder_39: pin names not known; wires that end beside it: A_2[11], multiplexer_77_out, full_adder_39_p3, full_adder_37_p3, full_adder_39_p5
  or or_39 (or_39_out, B_2[11], A_2[11]);
  xor xor_41 (xor_41_out, B_2[11], A_2[11]);
  Multiplexer #(.Selector_Bits(3)) multiplexer_79 (
    .sel(F_2), .in_0(full_adder_39_p5), .in_1(full_adder_39_p5), .in_2(xor_41_out), .in_3(or_39_out),
    .in_4(and_41_out), .in_5(barrelshifter_1_out), .in_6(barrelshifter_1_out), .in_7(barrelshifter_1_out),
    .out(R_2[11]));
  not not_40 (not_40_out, B[13]);
  and and_42 (and_42_out, B[13], A[13]);
  Multiplexer multiplexer_80 (.sel(full_adder_64_p3), .in_0(B[13]), .in_1(not_40_out), .out(multiplexer_80_out));
  // full_adder full_adder_40: pin names not known; wires that end beside it: A[13], multiplexer_80_out, full_adder_40_p3, full_adder_38_p3, full_adder_40_p5
  or or_40 (or_40_out, B[13], A[13]);
  not not_41 (not_41_out, B_2[10]);
  Multiplexer multiplexer_81 (.sel(full_adder_61_p3), .in_0(B_2[10]), .in_1(not_41_out), .out(multiplexer_81_out));
  and and_43 (and_43_out, B_2[10], A_2[10]);
  xor xor_42 (xor_42_out, B[13], A[13]);
  // full_adder full_adder_41: pin names not known; wires that end beside it: A_2[10], multiplexer_81_out, full_adder_41_p3, full_adder_39_p3, full_adder_41_p5
  or or_41 (or_41_out, B_2[10], A_2[10]);
  Multiplexer #(.Selector_Bits(3)) multiplexer_82 (
    .sel(F), .in_0(full_adder_40_p5), .in_1(full_adder_40_p5), .in_2(xor_42_out), .in_3(or_40_out),
    .in_4(and_42_out), .in_5(1'b0), .in_6(1'b0), .in_7(1'b0), .out(multiplexer_129_out[13]));
  xor xor_43 (xor_43_out, B_2[10], A_2[10]);
  Multiplexer #(.Selector_Bits(3)) multiplexer_83 (
    .sel(F_2), .in_0(full_adder_41_p5), .in_1(full_adder_41_p5), .in_2(xor_43_out), .in_3(or_41_out),
    .in_4(and_43_out), .in_5(barrelshifter_1_out), .in_6(barrelshifter_1_out), .in_7(barrelshifter_1_out),
    .out(R_2[10]));
  not not_42 (not_42_out, B[12]);
  Multiplexer multiplexer_84 (.sel(full_adder_64_p3), .in_0(B[12]), .in_1(not_42_out), .out(multiplexer_84_out));
  and and_44 (and_44_out, B[12], A[12]);
  not not_43 (not_43_out, B_2[9]);
  // full_adder full_adder_42: pin names not known; wires that end beside it: A[12], multiplexer_84_out, full_adder_42_p3, full_adder_40_p3, full_adder_42_p5
  or or_42 (or_42_out, B[12], A[12]);
  Multiplexer multiplexer_85 (.sel(full_adder_61_p3), .in_0(B_2[9]), .in_1(not_43_out), .out(multiplexer_85_out));
  and and_45 (and_45_out, B_2[9], A_2[9]);
  xor xor_44 (xor_44_out, B[12], A[12]);
  Multiplexer #(.Selector_Bits(3)) multiplexer_86 (
    .sel(F), .in_0(full_adder_42_p5), .in_1(full_adder_42_p5), .in_2(xor_44_out), .in_3(or_42_out),
    .in_4(and_44_out), .in_5(1'b0), .in_6(1'b0), .in_7(1'b0), .out(multiplexer_129_out[12]));
  // full_adder full_adder_43: pin names not known; wires that end beside it: A_2[9], multiplexer_85_out, full_adder_43_p3, full_adder_41_p3, full_adder_43_p5
  or or_43 (or_43_out, B_2[9], A_2[9]);
  xor xor_45 (xor_45_out, B_2[9], A_2[9]);
  Multiplexer #(.Selector_Bits(3)) multiplexer_87 (
    .sel(F_2), .in_0(full_adder_43_p5), .in_1(full_adder_43_p5), .in_2(xor_45_out), .in_3(or_43_out),
    .in_4(and_45_out), .in_5(barrelshifter_1_out), .in_6(barrelshifter_1_out), .in_7(barrelshifter_1_out),
    .out(R_2[9]));
  not not_44 (not_44_out, B[11]);
  and and_46 (and_46_out, B[11], A[11]);
  Multiplexer multiplexer_88 (.sel(full_adder_64_p3), .in_0(B[11]), .in_1(not_44_out), .out(multiplexer_88_out));
  // full_adder full_adder_44: pin names not known; wires that end beside it: A[11], multiplexer_88_out, full_adder_44_p3, full_adder_42_p3, full_adder_44_p5
  or or_44 (or_44_out, B[11], A[11]);
  not not_45 (not_45_out, B_2[8]);
  Multiplexer multiplexer_89 (.sel(full_adder_61_p3), .in_0(B_2[8]), .in_1(not_45_out), .out(multiplexer_89_out));
  and and_47 (and_47_out, B_2[8], A_2[8]);
  xor xor_46 (xor_46_out, B[11], A[11]);
  // full_adder full_adder_45: pin names not known; wires that end beside it: A_2[8], multiplexer_89_out, full_adder_45_p3, full_adder_43_p3, full_adder_45_p5
  or or_45 (or_45_out, B_2[8], A_2[8]);
  Multiplexer #(.Selector_Bits(3)) multiplexer_90 (
    .sel(F), .in_0(full_adder_44_p5), .in_1(full_adder_44_p5), .in_2(xor_46_out), .in_3(or_44_out),
    .in_4(and_46_out), .in_5(1'b0), .in_6(1'b0), .in_7(1'b0), .out(multiplexer_129_out[11]));
  xor xor_47 (xor_47_out, B_2[8], A_2[8]);
  Multiplexer #(.Selector_Bits(3)) multiplexer_91 (
    .sel(F_2), .in_0(full_adder_45_p5), .in_1(full_adder_45_p5), .in_2(xor_47_out), .in_3(or_45_out),
    .in_4(and_47_out), .in_5(barrelshifter_1_out), .in_6(barrelshifter_1_out), .in_7(barrelshifter_1_out),
    .out(R_2[8]));
  not not_46 (not_46_out, B[10]);
  Multiplexer multiplexer_92 (.sel(full_adder_64_p3), .in_0(B[10]), .in_1(not_46_out), .out(multiplexer_92_out));
  and and_48 (and_48_out, B[10], A[10]);
  not not_47 (not_47_out, B_2[7]);
  // full_adder full_adder_46: pin names not known; wires that end beside it: A[10], multiplexer_92_out, full_adder_46_p3, full_adder_44_p3, full_adder_46_p5
  or or_46 (or_46_out, B[10], A[10]);
  Multiplexer multiplexer_93 (.sel(full_adder_61_p3), .in_0(B_2[7]), .in_1(not_47_out), .out(multiplexer_93_out));
  and and_49 (and_49_out, B_2[7], A_2[7]);
  xor xor_48 (xor_48_out, B[10], A[10]);
  Multiplexer #(.Selector_Bits(3)) multiplexer_94 (
    .sel(F), .in_0(full_adder_46_p5), .in_1(full_adder_46_p5), .in_2(xor_48_out), .in_3(or_46_out),
    .in_4(and_48_out), .in_5(1'b0), .in_6(1'b0), .in_7(1'b0), .out(multiplexer_129_out[10]));
  // full_adder full_adder_47: pin names not known; wires that end beside it: A_2[7], multiplexer_93_out, full_adder_47_p3, full_adder_45_p3, full_adder_47_p5
  or or_47 (or_47_out, B_2[7], A_2[7]);
  xor xor_49 (xor_49_out, B_2[7], A_2[7]);
  Multiplexer #(.Selector_Bits(3)) multiplexer_95 (
    .sel(F_2), .in_0(full_adder_47_p5), .in_1(full_adder_47_p5), .in_2(xor_49_out), .in_3(or_47_out),
    .in_4(and_49_out), .in_5(barrelshifter_1_out), .in_6(barrelshifter_1_out), .in_7(barrelshifter_1_out),
    .out(R_2[7]));
  not not_48 (not_48_out, B[9]);
  and and_50 (and_50_out, B[9], A[9]);
  Multiplexer multiplexer_96 (.sel(full_adder_64_p3), .in_0(B[9]), .in_1(not_48_out), .out(multiplexer_96_out));
  // full_adder full_adder_48: pin names not known; wires that end beside it: A[9], multiplexer_96_out, full_adder_48_p3, full_adder_46_p3, full_adder_48_p5
  or or_48 (or_48_out, B[9], A[9]);
  not not_49 (not_49_out, B_2[6]);
  Multiplexer multiplexer_97 (.sel(full_adder_61_p3), .in_0(B_2[6]), .in_1(not_49_out), .out(multiplexer_97_out));
  and and_51 (and_51_out, B_2[6], A_2[6]);
  xor xor_50 (xor_50_out, B[9], A[9]);
  // full_adder full_adder_49: pin names not known; wires that end beside it: A_2[6], multiplexer_97_out, full_adder_49_p3, full_adder_47_p3, full_adder_49_p5
  or or_49 (or_49_out, B_2[6], A_2[6]);
  Multiplexer #(.Selector_Bits(3)) multiplexer_98 (
    .sel(F), .in_0(full_adder_48_p5), .in_1(full_adder_48_p5), .in_2(xor_50_out), .in_3(or_48_out),
    .in_4(and_50_out), .in_5(1'b0), .in_6(1'b0), .in_7(1'b0), .out(multiplexer_129_out[9]));
  xor xor_51 (xor_51_out, B_2[6], A_2[6]);
  Multiplexer #(.Selector_Bits(3)) multiplexer_99 (
    .sel(F_2), .in_0(full_adder_49_p5), .in_1(full_adder_49_p5), .in_2(xor_51_out), .in_3(or_49_out),
    .in_4(and_51_out), .in_5(barrelshifter_1_out), .in_6(barrelshifter_1_out), .in_7(barrelshifter_1_out),
    .out(R_2[6]));
  not not_50 (not_50_out, B[8]);
  Multiplexer multiplexer_100 (.sel(full_adder_64_p3), .in_0(B[8]), .in_1(not_50_out), .out(multiplexer_100_out));
  and and_52 (and_52_out, B[8], A[8]);
  not not_51 (not_51_out, B_2[5]);
  // full_adder full_adder_50: pin names not known; wires that end beside it: A[8], multiplexer_100_out, full_adder_50_p3, full_adder_48_p3, full_adder_50_p5
  or or_50 (or_50_out, B[8], A[8]);
  Multiplexer multiplexer_101 (.sel(full_adder_61_p3), .in_0(B_2[5]), .in_1(not_51_out), .out(multiplexer_101_out));
  and and_53 (and_53_out, B_2[5], A_2[5]);
  xor xor_52 (xor_52_out, B[8], A[8]);
  Multiplexer #(.Selector_Bits(3)) multiplexer_102 (
    .sel(F), .in_0(full_adder_50_p5), .in_1(full_adder_50_p5), .in_2(xor_52_out), .in_3(or_50_out),
    .in_4(and_52_out), .in_5(1'b0), .in_6(1'b0), .in_7(1'b0), .out(multiplexer_129_out[8]));
  // full_adder full_adder_51: pin names not known; wires that end beside it: A_2[5], multiplexer_101_out, full_adder_51_p3, full_adder_49_p3, full_adder_51_p5
  or or_51 (or_51_out, B_2[5], A_2[5]);
  xor xor_53 (xor_53_out, B_2[5], A_2[5]);
  Multiplexer #(.Selector_Bits(3)) multiplexer_103 (
    .sel(F_2), .in_0(full_adder_51_p5), .in_1(full_adder_51_p5), .in_2(xor_53_out), .in_3(or_51_out),
    .in_4(and_53_out), .in_5(barrelshifter_1_out), .in_6(barrelshifter_1_out), .in_7(barrelshifter_1_out),
    .out(R_2[5]));
  not not_52 (not_52_out, B[7]);
  and and_54 (and_54_out, B[7], A[7]);
  Multiplexer multiplexer_104 (.sel(full_adder_64_p3), .in_0(B[7]), .in_1(not_52_out), .out(multiplexer_104_out));
  // full_adder full_adder_52: pin names not known; wires that end beside it: A[7], multiplexer_104_out, full_adder_52_p3, full_adder_50_p3, full_adder_52_p5
  or or_52 (or_52_out, B[7], A[7]);
  not not_53 (not_53_out, B_2[4]);
  Multiplexer multiplexer_105 (.sel(full_adder_61_p3), .in_0(B_2[4]), .in_1(not_53_out), .out(multiplexer_105_out));
  and and_55 (and_55_out, B_2[4], A_2[4]);
  xor xor_54 (xor_54_out, B[7], A[7]);
  // full_adder full_adder_53: pin names not known; wires that end beside it: A_2[4], multiplexer_105_out, full_adder_53_p3, full_adder_51_p3, full_adder_53_p5
  or or_53 (or_53_out, B_2[4], A_2[4]);
  Multiplexer #(.Selector_Bits(3)) multiplexer_106 (
    .sel(F), .in_0(full_adder_52_p5), .in_1(full_adder_52_p5), .in_2(xor_54_out), .in_3(or_52_out),
    .in_4(and_54_out), .in_5(1'b0), .in_6(1'b0), .in_7(1'b0), .out(multiplexer_129_out[7]));
  xor xor_55 (xor_55_out, B_2[4], A_2[4]);
  Multiplexer #(.Selector_Bits(3)) multiplexer_107 (
    .sel(F_2), .in_0(full_adder_53_p5), .in_1(full_adder_53_p5), .in_2(xor_55_out), .in_3(or_53_out),
    .in_4(and_55_out), .in_5(barrelshifter_1_out), .in_6(barrelshifter_1_out), .in_7(barrelshifter_1_out),
    .out(R_2[4]));
  not not_54 (not_54_out, B[6]);
  Multiplexer multiplexer_108 (.sel(full_adder_64_p3), .in_0(B[6]), .in_1(not_54_out), .out(multiplexer_108_out));
  and and_56 (and_56_out, B[6], A[6]);
  not not_55 (not_55_out, B_2[3]);
  // full_adder full_adder_54: pin names not known; wires that end beside it: A[6], multiplexer_108_out, full_adder_54_p3, full_adder_52_p3, full_adder_54_p5
  or or_54 (or_54_out, B[6], A[6]);
  Multiplexer multiplexer_109 (.sel(full_adder_61_p3), .in_0(B_2[3]), .in_1(not_55_out), .out(multiplexer_109_out));
  and and_57 (and_57_out, B_2[3], A_2[3]);
  xor xor_56 (xor_56_out, B[6], A[6]);
  Multiplexer #(.Selector_Bits(3)) multiplexer_110 (
    .sel(F), .in_0(full_adder_54_p5), .in_1(full_adder_54_p5), .in_2(xor_56_out), .in_3(or_54_out),
    .in_4(and_56_out), .in_5(1'b0), .in_6(1'b0), .in_7(1'b0), .out(multiplexer_129_out[6]));
  // full_adder full_adder_55: pin names not known; wires that end beside it: A_2[3], multiplexer_109_out, full_adder_55_p3, full_adder_53_p3, full_adder_55_p5
  or or_55 (or_55_out, B_2[3], A_2[3]);
  xor xor_57 (xor_57_out, B_2[3], A_2[3]);
  Multiplexer #(.Selector_Bits(3)) multiplexer_111 (
    .sel(F_2), .in_0(full_adder_55_p5), .in_1(full_adder_55_p5), .in_2(xor_57_out), .in_3(or_55_out),
    .in_4(and_57_out), .in_5(barrelshifter_1_out), .in_6(barrelshifter_1_out), .in_7(barrelshifter_1_out),
    .out(R_2[3]));
  not not_56 (not_56_out, B[5]);
  and and_58 (and_58_out, B[5], A[5]);
  Multiplexer multiplexer_112 (.sel(full_adder_64_p3), .in_0(B[5]), .in_1(not_56_out), .out(multiplexer_112_out));
  // full_adder full_adder_56: pin names not known; wires that end beside it: A[5], multiplexer_112_out, full_adder_56_p3, full_adder_54_p3, full_adder_56_p5
  or or_56 (or_56_out, B[5], A[5]);
  not not_57 (not_57_out, B_2[2]);
  Multiplexer multiplexer_113 (.sel(full_adder_61_p3), .in_0(B_2[2]), .in_1(not_57_out), .out(multiplexer_113_out));
  and and_59 (and_59_out, B_2[2], A_2[2]);
  xor xor_58 (xor_58_out, B[5], A[5]);
  // full_adder full_adder_57: pin names not known; wires that end beside it: A_2[2], multiplexer_113_out, full_adder_57_p3, full_adder_55_p3, full_adder_57_p5
  or or_57 (or_57_out, B_2[2], A_2[2]);
  Multiplexer #(.Selector_Bits(3)) multiplexer_114 (
    .sel(F), .in_0(full_adder_56_p5), .in_1(full_adder_56_p5), .in_2(xor_58_out), .in_3(or_56_out),
    .in_4(and_58_out), .in_5(1'b0), .in_6(1'b0), .in_7(1'b0), .out(multiplexer_129_out[5]));
  xor xor_59 (xor_59_out, B_2[2], A_2[2]);
  Multiplexer #(.Selector_Bits(3)) multiplexer_115 (
    .sel(F_2), .in_0(full_adder_57_p5), .in_1(full_adder_57_p5), .in_2(xor_59_out), .in_3(or_57_out),
    .in_4(and_59_out), .in_5(barrelshifter_1_out), .in_6(barrelshifter_1_out), .in_7(barrelshifter_1_out),
    .out(R_2[2]));
  not not_58 (not_58_out, B[4]);
  Multiplexer multiplexer_116 (.sel(full_adder_64_p3), .in_0(B[4]), .in_1(not_58_out), .out(multiplexer_116_out));
  and and_60 (and_60_out, B[4], A[4]);
  not not_59 (not_59_out, B_2[1]);
  // full_adder full_adder_58: pin names not known; wires that end beside it: A[4], multiplexer_116_out, full_adder_58_p3, full_adder_56_p3, full_adder_58_p5
  or or_58 (or_58_out, B[4], A[4]);
  Multiplexer multiplexer_117 (.sel(full_adder_61_p3), .in_0(B_2[1]), .in_1(not_59_out), .out(multiplexer_117_out));
  and and_61 (and_61_out, B_2[1], A_2[1]);
  xor xor_60 (xor_60_out, B[4], A[4]);
  Multiplexer #(.Selector_Bits(3)) multiplexer_118 (
    .sel(F), .in_0(full_adder_58_p5), .in_1(full_adder_58_p5), .in_2(xor_60_out), .in_3(or_58_out),
    .in_4(and_60_out), .in_5(1'b0), .in_6(1'b0), .in_7(1'b0), .out(multiplexer_129_out[4]));
  // full_adder full_adder_59: pin names not known; wires that end beside it: A_2[1], multiplexer_117_out, full_adder_59_p3, full_adder_57_p3, full_adder_59_p5
  or or_59 (or_59_out, B_2[1], A_2[1]);
  xor xor_61 (xor_61_out, B_2[1], A_2[1]);
  Multiplexer #(.Selector_Bits(3)) multiplexer_119 (
    .sel(F_2), .in_0(full_adder_59_p5), .in_1(full_adder_59_p5), .in_2(xor_61_out), .in_3(or_59_out),
    .in_4(and_61_out), .in_5(barrelshifter_1_out), .in_6(barrelshifter_1_out), .in_7(barrelshifter_1_out),
    .out(R_2[1]));
  not not_60 (not_60_out, B[3]);
  and and_62 (and_62_out, B[3], A[3]);
  Multiplexer multiplexer_120 (.sel(full_adder_64_p3), .in_0(B[3]), .in_1(not_60_out), .out(multiplexer_120_out));
  // full_adder full_adder_60: pin names not known; wires that end beside it: A[3], multiplexer_120_out, full_adder_60_p3, full_adder_58_p3, full_adder_60_p5
  or or_60 (or_60_out, B[3], A[3]);
  not not_61 (not_61_out, B_2[0]);
  Multiplexer multiplexer_121 (.sel(full_adder_61_p3), .in_0(B_2[0]), .in_1(not_61_out), .out(multiplexer_121_out));
  and and_63 (and_63_out, B_2[0], A_2[0]);
  xor xor_62 (xor_62_out, B[3], A[3]);
  // full_adder full_adder_61: pin names not known; wires that end beside it: A_2[0], multiplexer_121_out, full_adder_61_p3, full_adder_59_p3, full_adder_61_p5
  or or_61 (or_61_out, B_2[0], A_2[0]);
  Multiplexer #(.Selector_Bits(3)) multiplexer_122 (
    .sel(F), .in_0(full_adder_60_p5), .in_1(full_adder_60_p5), .in_2(xor_62_out), .in_3(or_60_out),
    .in_4(and_62_out), .in_5(1'b0), .in_6(1'b0), .in_7(1'b0), .out(multiplexer_129_out[3]));
  and and_64 (full_adder_61_p3, F_2[0], not_63_out, not_62_out);
  xor xor_63 (xor_63_out, B_2[0], A_2[0]);
  Multiplexer #(.Selector_Bits(3)) multiplexer_123 (
    .sel(F_2), .in_0(full_adder_61_p5), .in_1(full_adder_61_p5), .in_2(xor_63_out), .in_3(or_61_out),
    .in_4(and_63_out), .in_5(barrelshifter_1_out), .in_6(barrelshifter_1_out), .in_7(barrelshifter_1_out),
    .out(R_2[0]));
  not not_62 (not_62_out, F_2[2]);
  not not_63 (not_63_out, F_2[1]);
  not not_64 (not_64_out, B[2]);
  Multiplexer multiplexer_124 (.sel(full_adder_64_p3), .in_0(B[2]), .in_1(not_64_out), .out(multiplexer_124_out));
  and and_65 (and_65_out, B[2], A[2]);
  // full_adder full_adder_62: pin names not known; wires that end beside it: A[2], multiplexer_124_out, full_adder_62_p3, full_adder_60_p3, full_adder_62_p5
  or or_62 (or_62_out, B[2], A[2]);
  xor xor_64 (xor_64_out, B[2], A[2]);
  Multiplexer #(.Selector_Bits(3)) multiplexer_125 (
    .sel(F), .in_0(full_adder_62_p5), .in_1(full_adder_62_p5), .in_2(xor_64_out), .in_3(or_62_out),
    .in_4(and_65_out), .in_5(1'b0), .in_6(1'b0), .in_7(1'b0), .out(multiplexer_129_out[2]));
  not not_65 (not_65_out, B[1]);
  and and_66 (and_66_out, B[1], A[1]);
  Multiplexer multiplexer_126 (.sel(full_adder_64_p3), .in_0(B[1]), .in_1(not_65_out), .out(multiplexer_126_out));
  // full_adder full_adder_63: pin names not known; wires that end beside it: A[1], multiplexer_126_out, full_adder_63_p3, full_adder_62_p3, full_adder_63_p5
  or or_63 (or_63_out, B[1], A[1]);
  xor xor_65 (xor_65_out, B[1], A[1]);
  BarrelShifter barrelshifter_1 (.in(A_2[0]), .shift(B_2), .out(barrelshifter_1_out));
  Multiplexer #(.Selector_Bits(3)) multiplexer_127 (
    .sel(F), .in_0(full_adder_63_p5), .in_1(full_adder_63_p5), .in_2(xor_65_out), .in_3(or_63_out),
    .in_4(and_66_out), .in_5(1'b0), .in_6(1'b0), .in_7(1'b0), .out(multiplexer_129_out[1]));
  not not_66 (not_66_out, B[0]);
  Multiplexer multiplexer_128 (.sel(full_adder_64_p3), .in_0(B[0]), .in_1(not_66_out), .out(multiplexer_128_out));
  and and_67 (and_67_out, B[0], A[0]);
  // full_adder full_adder_64: pin names not known; wires that end beside it: A[0], multiplexer_128_out, full_adder_64_p3, full_adder_63_p3, full_adder_64_p5
  or or_64 (or_64_out, B[0], A[0]);
  and and_68 (full_adder_64_p3, F[0], not_68_out, not_67_out);
  xor xor_66 (xor_66_out, B[0], A[0]);
  Multiplexer #(.Selector_Bits(3)) multiplexer_129 (
    .sel(F), .in_0(full_adder_64_p5), .in_1(full_adder_64_p5), .in_2(xor_66_out), .in_3(or_64_out),
    .in_4(and_67_out), .in_5(1'b0), .in_6(1'b0), .in_7(1'b0), .out(multiplexer_129_out[0]));
  not not_67 (not_67_out, F[2]);
  not not_68 (not_68_out, F[1]);
  not not_69 (not_69_out, F[1]);
  and and_69 (and_69_out, F[0], not_69_out, F[2]);
  BarrelShifter #(.Bits(32)) barrelshifter_2 (.in(A), .shift(B[5:0]), .out(barrelshifter_2_out));
  // Pins of 1 and 32 bits meet at A_2

  assign {R_2[31], R_2[29]} = {neg_2, R_2[30]};
endmodule
