// Digital circuit ula_32bits.dig as structural Verilog
module ula_32bits (
  input  [2:0] F,
  input  [31:0] A,
  input  [31:0] B,
  output neg,
  output overflow,
  output zero,
  output [31:0] R
);

  wire and_2_out, and_3_out, and_4_out, and_5_out, and_6_out, and_7_out, and_8_out, and_9_out, and_10_out,
       and_11_out, and_12_out, and_13_out, and_14_out, and_15_out, and_16_out, and_17_out, and_18_out,
       and_19_out, and_20_out, and_21_out, and_22_out, and_23_out, and_24_out, and_25_out, and_26_out,
       and_27_out, and_28_out, and_29_out, and_30_out, and_31_out, and_32_out, and_33_out, and_35_out,
       and_36_out, and_37_out, full_adder_1_p3, full_adder_1_p4, full_adder_1_p5, full_adder_2_p3,
       full_adder_2_p5, full_adder_3_p3, full_adder_3_p5, full_adder_4_p3, full_adder_4_p5, full_adder_5_p3,
       full_adder_5_p5, full_adder_6_p3, full_adder_6_p5, full_adder_7_p3, full_adder_7_p5, full_adder_8_p3,
       full_adder_8_p5, full_adder_9_p3, full_adder_9_p5, full_adder_10_p3, full_adder_10_p5,
       full_adder_11_p3, full_adder_11_p5, full_adder_12_p3, full_adder_12_p5, full_adder_13_p3,
       full_adder_13_p5, full_adder_14_p3, full_adder_14_p5, full_adder_15_p3, full_adder_15_p5,
       full_adder_16_p3, full_adder_16_p5, full_adder_17_p3, full_adder_17_p5, full_adder_18_p3,
       full_adder_18_p5, full_adder_19_p3, full_adder_19_p5, full_adder_20_p3, full_adder_20_p5,
       full_adder_21_p3, full_adder_21_p5, full_adder_22_p3, full_adder_22_p5, full_adder_23_p3,
       full_adder_23_p5, full_adder_24_p3, full_adder_24_p5, full_adder_25_p3, full_adder_25_p5,
       full_adder_26_p3, full_adder_26_p5, full_adder_27_p3, full_adder_27_p5, full_adder_28_p3,
       full_adder_28_p5, full_adder_29_p3, full_adder_29_p5, full_adder_30_p3, full_adder_30_p5,
       full_adder_31_p3, full_adder_31_p5, full_adder_32_p3, full_adder_32_p5, multiplexer_4_out,
       multiplexer_6_out, multiplexer_8_out, multiplexer_9_out, multiplexer_10_out, multiplexer_12_out,
       multiplexer_14_out, multiplexer_16_out, multiplexer_18_out, multiplexer_20_out, multiplexer_22_out,
       multiplexer_24_out, multiplexer_26_out, multiplexer_28_out, multiplexer_30_out, multiplexer_32_out,
       multiplexer_34_out, multiplexer_36_out, multiplexer_38_out, multiplexer_40_out, multiplexer_42_out,
       multiplexer_44_out, multiplexer_46_out, multiplexer_48_out, multiplexer_50_out, multiplexer_52_out,
       multiplexer_54_out, multiplexer_56_out, multiplexer_58_out, multiplexer_60_out, multiplexer_62_out,
       multiplexer_64_out, multiplexer_66_out, not_1_out, not_2_out, not_3_out, not_4_out, not_5_out,
       not_6_out, not_7_out, not_8_out, not_9_out, not_10_out, not_11_out, not_12_out, not_13_out,
       not_14_out, not_15_out, not_16_out, not_17_out, not_18_out, not_19_out, not_20_out, not_21_out,
       not_22_out, not_23_out, not_24_out, not_25_out, not_26_out, not_27_out, not_28_out, not_29_out,
       not_30_out, not_31_out, not_32_out, not_33_out, not_34_out, not_35_out, not_36_out, or_1_out,
       or_2_out, or_3_out, or_4_out, or_5_out, or_6_out, or_7_out, or_8_out, or_9_out, or_10_out, or_11_out,
       or_12_out, or_13_out, or_14_out, or_15_out, or_16_out, or_17_out, or_18_out, or_19_out, or_20_out,
       or_21_out, or_22_out, or_23_out, or_24_out, or_25_out, or_26_out, or_27_out, or_28_out, or_29_out,
       or_30_out, or_31_out, or_32_out, xor_2_out, xor_3_out, xor_4_out, xor_5_out, xor_6_out, xor_7_out,
       xor_8_out, xor_9_out, xor_10_out, xor_11_out, xor_12_out, xor_13_out, xor_14_out, xor_15_out,
       xor_16_out, xor_17_out, xor_18_out, xor_19_out, xor_20_out, xor_21_out, xor_22_out, xor_23_out,
       xor_24_out, xor_25_out, xor_26_out, xor_27_out, xor_28_out, xor_29_out, xor_30_out, xor_31_out,
       xor_32_out, xor_33_out;
  wire [30:0] multiplexer_65_out;
  wire [31:0] barrelshifter_1_out, barrelshifter_2_out, barrelshifter_3_out, multiplexer_1_out,
       multiplexer_2_out;

  and and_1 (zero, ~neg, ~multiplexer_65_out[30], ~multiplexer_9_out, ~multiplexer_65_out[28], ~multiplexer_65_out[27], ~multiplexer_65_out[26], ~multiplexer_65_out[25], ~multiplexer_65_out[24], ~multiplexer_65_out[23], ~multiplexer_65_out[22], ~multiplexer_65_out[21], ~multiplexer_65_out[20], ~multiplexer_65_out[19], ~multiplexer_65_out[18], ~multiplexer_65_out[17], ~multiplexer_65_out[16], ~multiplexer_65_out[15], ~multiplexer_65_out[14], ~multiplexer_65_out[13], ~multiplexer_65_out[12], ~multiplexer_65_out[11], ~multiplexer_65_out[10], ~multiplexer_65_out[9], ~multiplexer_65_out[8], ~multiplexer_65_out[7], ~multiplexer_65_out[6], ~multiplexer_65_out[5], ~multiplexer_65_out[4], ~multiplexer_65_out[3], ~multiplexer_65_out[2], ~multiplexer_65_out[1], ~multiplexer_65_out[0]);  // And
  xor xor_1 (overflow, full_adder_1_p3, full_adder_1_p4);
  Multiplexer #(.Bits(32)) multiplexer_1 (
    .sel(and_35_out), .in_0({neg, {2{multiplexer_65_out[30]}}, multiplexer_65_out[28:0]}),
    .in_1(barrelshifter_3_out), .out(multiplexer_1_out));
  Multiplexer #(.Bits(32)) multiplexer_2 (
    .sel(and_36_out), .in_0(multiplexer_1_out), .in_1(barrelshifter_2_out), .out(multiplexer_2_out));
  Multiplexer #(.Bits(32)) multiplexer_3 (
    .sel(and_37_out), .in_0(multiplexer_2_out), .in_1(barrelshifter_1_out), .out(R));
  not not_1 (not_1_out, B[31]);
  Multiplexer multiplexer_4 (.sel(full_adder_32_p3), .in_0(B[31]), .in_1(not_1_out), .out(multiplexer_4_out));
  and and_2 (and_2_out, B[31], A[31]);
  // full_adder full_adder_1: pin names not known; wires that end beside it: A[31], multiplexer_4_out, full_adder_1_p3, full_adder_1_p4, full_adder_1_p5
  or or_1 (or_1_out, B[31], A[31]);
  xor xor_2 (xor_2_out, B[31], A[31]);
  Multiplexer #(.Selector_Bits(3)) multiplexer_5 (
    .sel(F), .in_0(full_adder_1_p5), .in_1(full_adder_1_p5), .in_2(xor_2_out), .in_3(or_1_out),
    .in_4(and_2_out), .in_5(1'b0), .in_6(1'b0), .in_7(1'b0), .out(neg));
  not not_2 (not_2_out, B[30]);
  and and_3 (and_3_out, B[30], A[30]);
  Multiplexer multiplexer_6 (.sel(full_adder_32_p3), .in_0(B[30]), .in_1(not_2_out), .out(multiplexer_6_out));
  // full_adder full_adder_2: pin names not known; wires that end beside it: A[30], multiplexer_6_out, full_adder_2_p3, full_adder_1_p3, full_adder_2_p5
  or or_2 (or_2_out, B[30], A[30]);
  xor xor_3 (xor_3_out, B[30], A[30]);
  Multiplexer #(.Selector_Bits(3)) multiplexer_7 (
    .sel(F), .in_0(full_adder_2_p5), .in_1(full_adder_2_p5), .in_2(xor_3_out), .in_3(or_2_out),
    .in_4(and_3_out), .in_5(1'b0), .in_6(1'b0), .in_7(1'b0), .out(multiplexer_65_out[30]));
  not not_3 (not_3_out, B[29]);
  Multiplexer multiplexer_8 (.sel(full_adder_32_p3), .in_0(B[29]), .in_1(not_3_out), .out(multiplexer_8_out));
  and and_4 (and_4_out, B[29], A[29]);
  // full_adder full_adder_3: pin names not known; wires that end beside it: A[29], multiplexer_8_out, full_adder_3_p3, full_adder_2_p3, full_adder_3_p5
  or or_3 (or_3_out, B[29], A[29]);
  xor xor_4 (xor_4_out, B[29], A[29]);
  Multiplexer #(.Selector_Bits(3)) multiplexer_9 (
    .sel(F), .in_0(full_adder_3_p5), .in_1(full_adder_3_p5), .in_2(xor_4_out), .in_3(or_3_out),
    .in_4(and_4_out), .in_5(1'b0), .in_6(1'b0), .in_7(1'b0), .out(multiplexer_9_out));
  not not_4 (not_4_out, B[28]);
  and and_5 (and_5_out, B[28], A[28]);
  Multiplexer multiplexer_10 (.sel(full_adder_32_p3), .in_0(B[28]), .in_1(not_4_out), .out(multiplexer_10_out));
  // full_adder full_adder_4: pin names not known; wires that end beside it: A[28], multiplexer_10_out, full_adder_4_p3, full_adder_3_p3, full_adder_4_p5
  or or_4 (or_4_out, B[28], A[28]);
  xor xor_5 (xor_5_out, B[28], A[28]);
  Multiplexer #(.Selector_Bits(3)) multiplexer_11 (
    .sel(F), .in_0(full_adder_4_p5), .in_1(full_adder_4_p5), .in_2(xor_5_out), .in_3(or_4_out),
    .in_4(and_5_out), .in_5(1'b0), .in_6(1'b0), .in_7(1'b0), .out(multiplexer_65_out[28]));
  not not_5 (not_5_out, B[27]);
  Multiplexer multiplexer_12 (.sel(full_adder_32_p3), .in_0(B[27]), .in_1(not_5_out), .out(multiplexer_12_out));
  and and_6 (and_6_out, B[27], A[27]);
  // full_adder full_adder_5: pin names not known; wires that end beside it: A[27], multiplexer_12_out, full_adder_5_p3, full_adder_4_p3, full_adder_5_p5
  or or_5 (or_5_out, B[27], A[27]);
  xor xor_6 (xor_6_out, B[27], A[27]);
  Multiplexer #(.Selector_Bits(3)) multiplexer_13 (
    .sel(F), .in_0(full_adder_5_p5), .in_1(full_adder_5_p5), .in_2(xor_6_out), .in_3(or_5_out),
    .in_4(and_6_out), .in_5(1'b0), .in_6(1'b0), .in_7(1'b0), .out(multiplexer_65_out[27]));
  not not_6 (not_6_out, B[26]);
  and and_7 (and_7_out, B[26], A[26]);
  Multiplexer multiplexer_14 (.sel(full_adder_32_p3), .in_0(B[26]), .in_1(not_6_out), .out(multiplexer_14_out));
  // full_adder full_adder_6: pin names not known; wires that end beside it: A[26], multiplexer_14_out, full_adder_6_p3, full_adder_5_p3, full_adder_6_p5
  or or_6 (or_6_out, B[26], A[26]);
  xor xor_7 (xor_7_out, B[26], A[26]);
  Multiplexer #(.Selector_Bits(3)) multiplexer_15 (
    .sel(F), .in_0(full_adder_6_p5), .in_1(full_adder_6_p5), .in_2(xor_7_out), .in_3(or_6_out),
    .in_4(and_7_out), .in_5(1'b0), .in_6(1'b0), .in_7(1'b0), .out(multiplexer_65_out[26]));
  not not_7 (not_7_out, B[25]);
  Multiplexer multiplexer_16 (.sel(full_adder_32_p3), .in_0(B[25]), .in_1(not_7_out), .out(multiplexer_16_out));
  and and_8 (and_8_out, B[25], A[25]);
  // full_adder full_adder_7: pin names not known; wires that end beside it: A[25], multiplexer_16_out, full_adder_7_p3, full_adder_6_p3, full_adder_7_p5
  or or_7 (or_7_out, B[25], A[25]);
  xor xor_8 (xor_8_out, B[25], A[25]);
  Multiplexer #(.Selector_Bits(3)) multiplexer_17 (
    .sel(F), .in_0(full_adder_7_p5), .in_1(full_adder_7_p5), .in_2(xor_8_out), .in_3(or_7_out),
    .in_4(and_8_out), .in_5(1'b0), .in_6(1'b0), .in_7(1'b0), .out(multiplexer_65_out[25]));
  not not_8 (not_8_out, B[24]);
  and and_9 (and_9_out, B[24], A[24]);
  Multiplexer multiplexer_18 (.sel(full_adder_32_p3), .in_0(B[24]), .in_1(not_8_out), .out(multiplexer_18_out));
  // full_adder full_adder_8: pin names not known; wires that end beside it: A[24], multiplexer_18_out, full_adder_8_p3, full_adder_7_p3, full_adder_8_p5
  or or_8 (or_8_out, B[24], A[24]);
  xor xor_9 (xor_9_out, B[24], A[24]);
  Multiplexer #(.Selector_Bits(3)) multiplexer_19 (
    .sel(F), .in_0(full_adder_8_p5), .in_1(full_adder_8_p5), .in_2(xor_9_out), .in_3(or_8_out),
    .in_4(and_9_out), .in_5(1'b0), .in_6(1'b0), .in_7(1'b0), .out(multiplexer_65_out[24]));
  not not_9 (not_9_out, B[23]);
  Multiplexer multiplexer_20 (.sel(full_adder_32_p3), .in_0(B[23]), .in_1(not_9_out), .out(multiplexer_20_out));
  and and_10 (and_10_out, B[23], A[23]);
  // full_adder full_adder_9: pin names not known; wires that end beside it: A[23], multiplexer_20_out, full_adder_9_p3, full_adder_8_p3, full_adder_9_p5
  or or_9 (or_9_out, B[23], A[23]);
  xor xor_10 (xor_10_out, B[23], A[23]);
  Multiplexer #(.Selector_Bits(3)) multiplexer_21 (
    .sel(F), .in_0(full_adder_9_p5), .in_1(full_adder_9_p5), .in_2(xor_10_out), .in_3(or_9_out),
    .in_4(and_10_out), .in_5(1'b0), .in_6(1'b0), .in_7(1'b0), .out(multiplexer_65_out[23]));
  not not_10 (not_10_out, B[22]);
  and and_11 (and_11_out, B[22], A[22]);
  Multiplexer multiplexer_22 (.sel(full_adder_32_p3), .in_0(B[22]), .in_1(not_10_out), .out(multiplexer_22_out));
  // full_adder full_adder_10: pin names not known; wires that end beside it: A[22], multiplexer_22_out, full_adder_10_p3, full_adder_9_p3, full_adder_10_p5
  or or_10 (or_10_out, B[22], A[22]);
  xor xor_11 (xor_11_out, B[22], A[22]);
  Multiplexer #(.Selector_Bits(3)) multiplexer_23 (
    .sel(F), .in_0(full_adder_10_p5), .in_1(full_adder_10_p5), .in_2(xor_11_out), .in_3(or_10_out),
    .in_4(and_11_out), .in_5(1'b0), .in_6(1'b0), .in_7(1'b0), .out(multiplexer_65_out[22]));
  not not_11 (not_11_out, B[21]);
  Multiplexer multiplexer_24 (.sel(full_adder_32_p3), .in_0(B[21]), .in_1(not_11_out), .out(multiplexer_24_out));
  and and_12 (and_12_out, B[21], A[21]);
  // full_adder full_adder_11: pin names not known; wires that end beside it: A[21], multiplexer_24_out, full_adder_11_p3, full_adder_10_p3, full_adder_11_p5
  or or_11 (or_11_out, B[21], A[21]);
  xor xor_12 (xor_12_out, B[21], A[21]);
  Multiplexer #(.Selector_Bits(3)) multiplexer_25 (
    .sel(F), .in_0(full_adder_11_p5), .in_1(full_adder_11_p5), .in_2(xor_12_out), .in_3(or_11_out),
    .in_4(and_12_out), .in_5(1'b0), .in_6(1'b0), .in_7(1'b0), .out(multiplexer_65_out[21]));
  not not_12 (not_12_out, B[20]);
  and and_13 (and_13_out, B[20], A[20]);
  Multiplexer multiplexer_26 (.sel(full_adder_32_p3), .in_0(B[20]), .in_1(not_12_out), .out(multiplexer_26_out));
  // full_adder full_adder_12: pin names not known; wires that end beside it: A[20], multiplexer_26_out, full_adder_12_p3, full_adder_11_p3, full_adder_12_p5
  or or_12 (or_12_out, B[20], A[20]);
  xor xor_13 (xor_13_out, B[20], A[20]);
  Multiplexer #(.Selector_Bits(3)) multiplexer_27 (
    .sel(F), .in_0(full_adder_12_p5), .in_1(full_adder_12_p5), .in_2(xor_13_out), .in_3(or_12_out),
    .in_4(and_13_out), .in_5(1'b0), .in_6(1'b0), .in_7(1'b0), .out(multiplexer_65_out[20]));
  not not_13 (not_13_out, B[19]);
  Multiplexer multiplexer_28 (.sel(full_adder_32_p3), .in_0(B[19]), .in_1(not_13_out), .out(multiplexer_28_out));
  and and_14 (and_14_out, B[19], A[19]);
  // full_adder full_adder_13: pin names not known; wires that end beside it: A[19], multiplexer_28_out, full_adder_13_p3, full_adder_12_p3, full_adder_13_p5
  or or_13 (or_13_out, B[19], A[19]);
  xor xor_14 (xor_14_out, B[19], A[19]);
  Multiplexer #(.Selector_Bits(3)) multiplexer_29 (
    .sel(F), .in_0(full_adder_13_p5), .in_1(full_adder_13_p5), .in_2(xor_14_out), .in_3(or_13_out),
    .in_4(and_14_out), .in_5(1'b0), .in_6(1'b0), .in_7(1'b0), .out(multiplexer_65_out[19]));
  not not_14 (not_14_out, B[18]);
  and and_15 (and_15_out, B[18], A[18]);
  Multiplexer multiplexer_30 (.sel(full_adder_32_p3), .in_0(B[18]), .in_1(not_14_out), .out(multiplexer_30_out));
  // full_adder full_adder_14: pin names not known; wires that end beside it: A[18], multiplexer_30_out, full_adder_14_p3, full_adder_13_p3, full_adder_14_p5
  or or_14 (or_14_out, B[18], A[18]);
  xor xor_15 (xor_15_out, B[18], A[18]);
  Multiplexer #(.Selector_Bits(3)) multiplexer_31 (
    .sel(F), .in_0(full_adder_14_p5), .in_1(full_adder_14_p5), .in_2(xor_15_out), .in_3(or_14_out),
    .in_4(and_15_out), .in_5(1'b0), .in_6(1'b0), .in_7(1'b0), .out(multiplexer_65_out[18]));
  not not_15 (not_15_out, B[17]);
  Multiplexer multiplexer_32 (.sel(full_adder_32_p3), .in_0(B[17]), .in_1(not_15_out), .out(multiplexer_32_out));
  and and_16 (and_16_out, B[17], A[17]);
  // full_adder full_adder_15: pin names not known; wires that end beside it: A[17], multiplexer_32_out, full_adder_15_p3, full_adder_14_p3, full_adder_15_p5
  or or_15 (or_15_out, B[17], A[17]);
  xor xor_16 (xor_16_out, B[17], A[17]);
  Multiplexer #(.Selector_Bits(3)) multiplexer_33 (
    .sel(F), .in_0(full_adder_15_p5), .in_1(full_adder_15_p5), .in_2(xor_16_out), .in_3(or_15_out),
    .in_4(and_16_out), .in_5(1'b0), .in_6(1'b0), .in_7(1'b0), .out(multiplexer_65_out[17]));
  not not_16 (not_16_out, B[16]);
  and and_17 (and_17_out, B[16], A[16]);
  Multiplexer multiplexer_34 (.sel(full_adder_32_p3), .in_0(B[16]), .in_1(not_16_out), .out(multiplexer_34_out));
  // full_adder full_adder_16: pin names not known; wires that end beside it: A[16], multiplexer_34_out, full_adder_16_p3, full_adder_15_p3, full_adder_16_p5
  or or_16 (or_16_out, B[16], A[16]);
  xor xor_17 (xor_17_out, B[16], A[16]);
  Multiplexer #(.Selector_Bits(3)) multiplexer_35 (
    .sel(F), .in_0(full_adder_16_p5), .in_1(full_adder_16_p5), .in_2(xor_17_out), .in_3(or_16_out),
    .in_4(and_17_out), .in_5(1'b0), .in_6(1'b0), .in_7(1'b0), .out(multiplexer_65_out[16]));
  not not_17 (not_17_out, B[15]);
  Multiplexer multiplexer_36 (.sel(full_adder_32_p3), .in_0(B[15]), .in_1(not_17_out), .out(multiplexer_36_out));
  and and_18 (and_18_out, B[15], A[15]);
  // full_adder full_adder_17: pin names not known; wires that end beside it: A[15], multiplexer_36_out, full_adder_17_p3, full_adder_16_p3, full_adder_17_p5
  or or_17 (or_17_out, B[15], A[15]);
  xor xor_18 (xor_18_out, B[15], A[15]);
  Multiplexer #(.Selector_Bits(3)) multiplexer_37 (
    .sel(F), .in_0(full_adder_17_p5), .in_1(full_adder_17_p5), .in_2(xor_18_out), .in_3(or_17_out),
    .in_4(and_18_out), .in_5(1'b0), .in_6(1'b0), .in_7(1'b0), .out(multiplexer_65_out[15]));
  not not_18 (not_18_out, B[14]);
  and and_19 (and_19_out, B[14], A[14]);
  Multiplexer multiplexer_38 (.sel(full_adder_32_p3), .in_0(B[14]), .in_1(not_18_out), .out(multiplexer_38_out));
  // full_adder full_adder_18: pin names not known; wires that end beside it: A[14], multiplexer_38_out, full_adder_18_p3, full_adder_17_p3, full_adder_18_p5
  or or_18 (or_18_out, B[14], A[14]);
  xor xor_19 (xor_19_out, B[14], A[14]);
  Multiplexer #(.Selector_Bits(3)) multiplexer_39 (
    .sel(F), .in_0(full_adder_18_p5), .in_1(full_adder_18_p5), .in_2(xor_19_out), .in_3(or_18_out),
    .in_4(and_19_out), .in_5(1'b0), .in_6(1'b0), .in_7(1'b0), .out(multiplexer_65_out[14]));
  not not_19 (not_19_out, B[13]);
  Multiplexer multiplexer_40 (.sel(full_adder_32_p3), .in_0(B[13]), .in_1(not_19_out), .out(multiplexer_40_out));
  and and_20 (and_20_out, B[13], A[13]);
  // full_adder full_adder_19: pin names not known; wires that end beside it: A[13], multiplexer_40_out, full_adder_19_p3, full_adder_18_p3, full_adder_19_p5
  or or_19 (or_19_out, B[13], A[13]);
  xor xor_20 (xor_20_out, B[13], A[13]);
  Multiplexer #(.Selector_Bits(3)) multiplexer_41 (
    .sel(F), .in_0(full_adder_19_p5), .in_1(full_adder_19_p5), .in_2(xor_20_out), .in_3(or_19_out),
    .in_4(and_20_out), .in_5(1'b0), .in_6(1'b0), .in_7(1'b0), .out(multiplexer_65_out[13]));
  not not_20 (not_20_out, B[12]);
  and and_21 (and_21_out, B[12], A[12]);
  Multiplexer multiplexer_42 (.sel(full_adder_32_p3), .in_0(B[12]), .in_1(not_20_out), .out(multiplexer_42_out));
  // full_adder full_adder_20: pin names not known; wires that end beside it: A[12], multiplexer_42_out, full_adder_20_p3, full_adder_19_p3, full_adder_20_p5
  or or_20 (or_20_out, B[12], A[12]);
  xor xor_21 (xor_21_out, B[12], A[12]);
  Multiplexer #(.Selector_Bits(3)) multiplexer_43 (
    .sel(F), .in_0(full_adder_20_p5), .in_1(full_adder_20_p5), .in_2(xor_21_out), .in_3(or_20_out),
    .in_4(and_21_out), .in_5(1'b0), .in_6(1'b0), .in_7(1'b0), .out(multiplexer_65_out[12]));
  not not_21 (not_21_out, B[11]);
  Multiplexer multiplexer_44 (.sel(full_adder_32_p3), .in_0(B[11]), .in_1(not_21_out), .out(multiplexer_44_out));
  and and_22 (and_22_out, B[11], A[11]);
  // full_adder full_adder_21: pin names not known; wires that end beside it: A[11], multiplexer_44_out, full_adder_21_p3, full_adder_20_p3, full_adder_21_p5
  or or_21 (or_21_out, B[11], A[11]);
  xor xor_22 (xor_22_out, B[11], A[11]);
  Multiplexer #(.Selector_Bits(3)) multiplexer_45 (
    .sel(F), .in_0(full_adder_21_p5), .in_1(full_adder_21_p5), .in_2(xor_22_out), .in_3(or_21_out),
    .in_4(and_22_out), .in_5(1'b0), .in_6(1'b0), .in_7(1'b0), .out(multiplexer_65_out[11]));
  not not_22 (not_22_out, B[10]);
  and and_23 (and_23_out, B[10], A[10]);
  Multiplexer multiplexer_46 (.sel(full_adder_32_p3), .in_0(B[10]), .in_1(not_22_out), .out(multiplexer_46_out));
  // full_adder full_adder_22: pin names not known; wires that end beside it: A[10], multiplexer_46_out, full_adder_22_p3, full_adder_21_p3, full_adder_22_p5
  or or_22 (or_22_out, B[10], A[10]);
  xor xor_23 (xor_23_out, B[10], A[10]);
  Multiplexer #(.Selector_Bits(3)) multiplexer_47 (
    .sel(F), .in_0(full_adder_22_p5), .in_1(full_adder_22_p5), .in_2(xor_23_out), .in_3(or_22_out),
    .in_4(and_23_out), .in_5(1'b0), .in_6(1'b0), .in_7(1'b0), .out(multiplexer_65_out[10]));
  not not_23 (not_23_out, B[9]);
  Multiplexer multiplexer_48 (.sel(full_adder_32_p3), .in_0(B[9]), .in_1(not_23_out), .out(multiplexer_48_out));
  and and_24 (and_24_out, B[9], A[9]);
  // full_adder full_adder_23: pin names not known; wires that end beside it: A[9], multiplexer_48_out, full_adder_23_p3, full_adder_22_p3, full_adder_23_p5
  or or_23 (or_23_out, B[9], A[9]);
  xor xor_24 (xor_24_out, B[9], A[9]);
  Multiplexer #(.Selector_Bits(3)) multiplexer_49 (
    .sel(F), .in_0(full_adder_23_p5), .in_1(full_adder_23_p5), .in_2(xor_24_out), .in_3(or_23_out),
    .in_4(and_24_out), .in_5(1'b0), .in_6(1'b0), .in_7(1'b0), .out(multiplexer_65_out[9]));
  not not_24 (not_24_out, B[8]);
  and and_25 (and_25_out, B[8], A[8]);
  Multiplexer multiplexer_50 (.sel(full_adder_32_p3), .in_0(B[8]), .in_1(not_24_out), .out(multiplexer_50_out));
  // full_adder full_adder_24: pin names not known; wires that end beside it: A[8], multiplexer_50_out, full_adder_24_p3, full_adder_23_p3, full_adder_24_p5
  or or_24 (or_24_out, B[8], A[8]);
  xor xor_25 (xor_25_out, B[8], A[8]);
  Multiplexer #(.Selector_Bits(3)) multiplexer_51 (
    .sel(F), .in_0(full_adder_24_p5), .in_1(full_adder_24_p5), .in_2(xor_25_out), .in_3(or_24_out),
    .in_4(and_25_out), .in_5(1'b0), .in_6(1'b0), .in_7(1'b0), .out(multiplexer_65_out[8]));
  not not_25 (not_25_out, B[7]);
  Multiplexer multiplexer_52 (.sel(full_adder_32_p3), .in_0(B[7]), .in_1(not_25_out), .out(multiplexer_52_out));
  and and_26 (and_26_out, B[7], A[7]);
  // full_adder full_adder_25: pin names not known; wires that end beside it: A[7], multiplexer_52_out, full_adder_25_p3, full_adder_24_p3, full_adder_25_p5
  or or_25 (or_25_out, B[7], A[7]);
  xor xor_26 (xor_26_out, B[7], A[7]);
  Multiplexer #(.Selector_Bits(3)) multiplexer_53 (
    .sel(F), .in_0(full_adder_25_p5), .in_1(full_adder_25_p5), .in_2(xor_26_out), .in_3(or_25_out),
    .in_4(and_26_out), .in_5(1'b0), .in_6(1'b0), .in_7(1'b0), .out(multiplexer_65_out[7]));
  not not_26 (not_26_out, B[6]);
  and and_27 (and_27_out, B[6], A[6]);
  Multiplexer multiplexer_54 (.sel(full_adder_32_p3), .in_0(B[6]), .in_1(not_26_out), .out(multiplexer_54_out));
  // full_adder full_adder_26: pin names not known; wires that end beside it: A[6], multiplexer_54_out, full_adder_26_p3, full_adder_25_p3, full_adder_26_p5
  or or_26 (or_26_out, B[6], A[6]);
  xor xor_27 (xor_27_out, B[6], A[6]);
  Multiplexer #(.Selector_Bits(3)) multiplexer_55 (
    .sel(F), .in_0(full_adder_26_p5), .in_1(full_adder_26_p5), .in_2(xor_27_out), .in_3(or_26_out),
    .in_4(and_27_out), .in_5(1'b0), .in_6(1'b0), .in_7(1'b0), .out(multiplexer_65_out[6]));
  not not_27 (not_27_out, B[5]);
  Multiplexer multiplexer_56 (.sel(full_adder_32_p3), .in_0(B[5]), .in_1(not_27_out), .out(multiplexer_56_out));
  and and_28 (and_28_out, B[5], A[5]);
  // full_adder full_adder_27: pin names not known; wires that end beside it: A[5], multiplexer_56_out, full_adder_27_p3, full_adder_26_p3, full_adder_27_p5
  or or_27 (or_27_out, B[5], A[5]);
  xor xor_28 (xor_28_out, B[5], A[5]);
  Multiplexer #(.Selector_Bits(3)) multiplexer_57 (
    .sel(F), .in_0(full_adder_27_p5), .in_1(full_adder_27_p5), .in_2(xor_28_out), .in_3(or_27_out),
    .in_4(and_28_out), .in_5(1'b0), .in_6(1'b0), .in_7(1'b0), .out(multiplexer_65_out[5]));
  not not_28 (not_28_out, B[4]);
  and and_29 (and_29_out, B[4], A[4]);
  Multiplexer multiplexer_58 (.sel(full_adder_32_p3), .in_0(B[4]), .in_1(not_28_out), .out(multiplexer_58_out));
  // full_adder full_adder_28: pin names not known; wires that end beside it: A[4], multiplexer_58_out, full_adder_28_p3, full_adder_27_p3, full_adder_28_p5
  or or_28 (or_28_out, B[4], A[4]);
  xor xor_29 (xor_29_out, B[4], A[4]);
  Multiplexer #(.Selector_Bits(3)) multiplexer_59 (
    .sel(F), .in_0(full_adder_28_p5), .in_1(full_adder_28_p5), .in_2(xor_29_out), .in_3(or_28_out),
    .in_4(and_29_out), .in_5(1'b0), .in_6(1'b0), .in_7(1'b0), .out(multiplexer_65_out[4]));
  not not_29 (not_29_out, B[3]);
  Multiplexer multiplexer_60 (.sel(full_adder_32_p3), .in_0(B[3]), .in_1(not_29_out), .out(multiplexer_60_out));
  and and_30 (and_30_out, B[3], A[3]);
  // full_adder full_adder_29: pin names not known; wires that end beside it: A[3], multiplexer_60_out, full_adder_29_p3, full_adder_28_p3, full_adder_29_p5
  or or_29 (or_29_out, B[3], A[3]);
  xor xor_30 (xor_30_out, B[3], A[3]);
  Multiplexer #(.Selector_Bits(3)) multiplexer_61 (
    .sel(F), .in_0(full_adder_29_p5), .in_1(full_adder_29_p5), .in_2(xor_30_out), .in_3(or_29_out),
    .in_4(and_30_out), .in_5(1'b0), .in_6(1'b0), .in_7(1'b0), .out(multiplexer_65_out[3]));
  not not_30 (not_30_out, B[2]);
  and and_31 (and_31_out, B[2], A[2]);
  Multiplexer multiplexer_62 (.sel(full_adder_32_p3), .in_0(B[2]), .in_1(not_30_out), .out(multiplexer_62_out));
  // full_adder full_adder_30: pin names not known; wires that end beside it: A[2], multiplexer_62_out, full_adder_30_p3, full_adder_29_p3, full_adder_30_p5
  or or_30 (or_30_out, B[2], A[2]);
  xor xor_31 (xor_31_out, B[2], A[2]);
  Multiplexer #(.Selector_Bits(3)) multiplexer_63 (
    .sel(F), .in_0(full_adder_30_p5), .in_1(full_adder_30_p5), .in_2(xor_31_out), .in_3(or_30_out),
    .in_4(and_31_out), .in_5(1'b0), .in_6(1'b0), .in_7(1'b0), .out(multiplexer_65_out[2]));
  not not_31 (not_31_out, B[1]);
  Multiplexer multiplexer_64 (.sel(full_adder_32_p3), .in_0(B[1]), .in_1(not_31_out), .out(multiplexer_64_out));
  and and_32 (and_32_out, B[1], A[1]);
  // full_adder full_adder_31: pin names not known; wires that end beside it: A[1], multiplexer_64_out, full_adder_31_p3, full_adder_30_p3, full_adder_31_p5
  or or_31 (or_31_out, B[1], A[1]);
  xor xor_32 (xor_32_out, B[1], A[1]);
  Multiplexer #(.Selector_Bits(3)) multiplexer_65 (
    .sel(F), .in_0(full_adder_31_p5), .in_1(full_adder_31_p5), .in_2(xor_32_out), .in_3(or_31_out),
    .in_4(and_32_out), .in_5(1'b0), .in_6(1'b0), .in_7(1'b0), .out(multiplexer_65_out[1]));
  not not_32 (not_32_out, B[0]);
  and and_33 (and_33_out, B[0], A[0]);
  Multiplexer multiplexer_66 (.sel(full_adder_32_p3), .in_0(B[0]), .in_1(not_32_out), .out(multiplexer_66_out));
  // full_adder full_adder_32: pin names not known; wires that end beside it: A[0], multiplexer_66_out, full_adder_32_p3, full_adder_31_p3, full_adder_32_p5
  or or_32 (or_32_out, B[0], A[0]);
  and and_34 (full_adder_32_p3, F[0], not_34_out, not_33_out);
  xor xor_33 (xor_33_out, B[0], A[0]);
  Multiplexer #(.Selector_Bits(3)) multiplexer_67 (
    .sel(F), .in_0(full_adder_32_p5), .in_1(full_adder_32_p5), .in_2(xor_33_out), .in_3(or_32_out),
    .in_4(and_33_out), .in_5(1'b0), .in_6(1'b0), .in_7(1'b0), .out(multiplexer_65_out[0]));
  not not_33 (not_33_out, F[2]);
  not not_34 (not_34_out, F[1]);
  not not_35 (not_35_out, F[1]);
  and and_35 (and_35_out, F[0], not_35_out, F[2]);
  not not_36 (not_36_out, F[0]);
  and and_36 (and_36_out, not_36_out, F[1], F[2]);
  BarrelShifter #(.Bits(32), .barrelShifterMode("arithmetic"), .direction("right")) barrelshifter_1 (
    .in(A), .shift(B[5:0]), .out(barrelshifter_1_out));
  BarrelShifter #(.Bits(32), .direction("right")) barrelshifter_2 (.in(A), .shift(B[5:0]), .out(barrelshifter_2_out));
  BarrelShifter #(.Bits(32)) barrelshifter_3 (.in(A), .shift(B[5:0]), .out(barrelshifter_3_out));
  and and_37 (and_37_out, F[0], F[1], F[2]);

  // Notes on the sheet:
  //   sra
  //   srl
  //   sll
endmodule
